// Logisim project 8.bit_ALU.0.circ as structural Verilog: 1 circuit, main circuit main
module main (
  input  [7:0] in_1,
  input  in_2,
  input  [7:0] in_3,
  input  [3:0] in_4
);

  wire [3:0] bitselector_1_out, bitselector_2_out;
  wire [7:0] adder_1_out, and_1_out, demultiplexer_1_out0, demultiplexer_1_out1, demultiplexer_1_out2,
       demultiplexer_1_out3, demultiplexer_1_out4, demultiplexer_1_out5, demultiplexer_1_out6,
       demultiplexer_1_out7, demultiplexer_1_out8, demultiplexer_2_out0, demultiplexer_2_out1,
       demultiplexer_2_out2, demultiplexer_2_out3, demultiplexer_2_out4, demultiplexer_2_out5,
       demultiplexer_2_out6, demultiplexer_2_out7, multiplexer_1_out, nand_1_out, nor_1_out, or_1_out,
       shifter_1_out, subtractor_1_out, xnor_1_out, xor_1_out;

  Demultiplexer #(.select(4), .width(8)) demultiplexer_1 (
    .out0(demultiplexer_1_out0), .out1(demultiplexer_1_out1), .out2(demultiplexer_1_out2),
    .out3(demultiplexer_1_out3), .out4(demultiplexer_1_out4), .out5(demultiplexer_1_out5),
    .out6(demultiplexer_1_out6), .out7(demultiplexer_1_out7), .out8(demultiplexer_1_out8), .in(in_1),
    .sel(in_4));  // open: out9, out10, out11, out12, out13, out14, out15
  Demultiplexer #(.select(4), .width(8)) demultiplexer_2 (
    .out0(demultiplexer_2_out0), .out1(demultiplexer_2_out1), .out2(demultiplexer_2_out2),
    .out3(demultiplexer_2_out3), .out4(demultiplexer_2_out4), .out5(demultiplexer_2_out5),
    .out6(demultiplexer_2_out6), .out7(demultiplexer_2_out7), .in(in_3), .sel(in_4));  // open: out8, out9, out10, out11, out12, out13, out14, out15
  Adder adder_1 (.a(demultiplexer_1_out0), .b(demultiplexer_2_out0), .out(adder_1_out));  // open: cin, cout
  Subtractor subtractor_1 (
    .a(demultiplexer_1_out1), .b(demultiplexer_2_out1), .out(subtractor_1_out));  // open: bin, bout
  Shifter #(.shift("lr")) shifter_1 (.in(demultiplexer_1_out8), .\dist (3'b001), .out(shifter_1_out));
  assign and_1_out = demultiplexer_1_out2 & demultiplexer_2_out2;  // AND_Gate and_1, 8 bits wide
  assign nand_1_out = ~(demultiplexer_1_out3 & demultiplexer_2_out3);  // NAND_Gate nand_1, 8 bits wide
  assign or_1_out = demultiplexer_1_out4 | demultiplexer_2_out4;  // OR_Gate or_1, 8 bits wide
  assign nor_1_out = ~(demultiplexer_1_out5 | demultiplexer_2_out5);  // NOR_Gate nor_1, 8 bits wide
  assign xor_1_out = demultiplexer_1_out6 ^ demultiplexer_2_out6;  // XOR_Gate xor_1, 8 bits wide
  assign xnor_1_out = ~(demultiplexer_1_out7 ^ demultiplexer_2_out7);  // XNOR_Gate xnor_1, 8 bits wide
  Multiplexer #(.select(4), .width(8)) multiplexer_1 (
    .in0(adder_1_out), .in1(subtractor_1_out), .in2(and_1_out), .in3(nand_1_out), .in4(or_1_out),
    .in5(nor_1_out), .in6(xor_1_out), .in7(xnor_1_out), .in8(shifter_1_out), .out(multiplexer_1_out),
    .sel(in_4));  // open: in9, in10, in11, in12, in13, in14, in15
  Hex_Digit_Display hex_digit_display_1 (.value(bitselector_1_out));  // open: dp
  BitSelector #(.group(4)) bitselector_1 (.in(multiplexer_1_out), .out(bitselector_1_out), .sel(1'b1));
  Hex_Digit_Display hex_digit_display_2 (.value(bitselector_2_out));  // open: dp
  BitSelector #(.group(4)) bitselector_2 (.in(multiplexer_1_out), .out(bitselector_2_out), .sel(in_2));
endmodule
