// Logisim project 8.bit_ALU.SDR.ROM.0.circ as structural Verilog: 1 circuit, main circuit main
module main (
  input  [7:0] in_1,
  input  [3:0] in_2,
  input  [3:0] in_3,
  input  [3:0] in_4,
  input  [3:0] in_5,
  input  in_6
);

  wire bitselector_4_out, demultiplexer_2_out1, demultiplexer_2_out2, demultiplexer_2_out3,
       demultiplexer_2_out4, demultiplexer_2_out5, demultiplexer_2_out6, demultiplexer_2_out7,
       demultiplexer_2_out8, demultiplexer_2_out9, demultiplexer_2_out10, demultiplexer_2_out11,
       demultiplexer_2_out12, demultiplexer_2_out13, demultiplexer_2_out14, demultiplexer_2_out15;
  wire [2:0] bitselector_1_out;
  wire [3:0] bitselector_2_out, bitselector_3_out, bitselector_5_out, bitselector_6_out, bitselector_7_out,
       bitselector_8_out;
  wire [7:0] adder_1_out, and_1_out, buffer_1_out, demultiplexer_1_out1, demultiplexer_1_out2,
       demultiplexer_1_out3, demultiplexer_1_out4, demultiplexer_1_out5, demultiplexer_1_out6,
       demultiplexer_1_out7, demultiplexer_1_out8, demultiplexer_1_out9, demultiplexer_1_out10,
       demultiplexer_1_out11, demultiplexer_1_out12, demultiplexer_1_out13, demultiplexer_1_out14,
       demultiplexer_1_out15, demultiplexer_3_out0, demultiplexer_3_out1, demultiplexer_3_out2,
       demultiplexer_3_out3, demultiplexer_3_out4, demultiplexer_3_out5, demultiplexer_4_out0,
       demultiplexer_4_out1, demultiplexer_4_out2, demultiplexer_4_out3, demultiplexer_4_out4,
       multiplexer_1_out, multiplexer_2_out, multiplexer_3_out, multiplexer_4_out, multiplexer_5_out,
       or_1_out, register_1_q, register_2_q, register_3_q, register_4_q, register_5_q, register_6_q,
       register_7_q, register_8_q, register_9_q, register_10_q, register_11_q, register_12_q, register_13_q,
       register_14_q, register_15_q, rom_1_data, shifter_1_out, subtractor_1_out, undriven, xor_1_out;

  ROM #(.addrWidth(4)) rom_1 (.addr(in_2), .data(rom_1_data));
  BitSelector #(.group(3)) bitselector_1 (.in(rom_1_data), .out(bitselector_1_out), .sel(2'b00));
  Hex_Digit_Display hex_digit_display_1 (.value(bitselector_2_out));  // open: dp
  Hex_Digit_Display hex_digit_display_2 (.value(bitselector_3_out));  // open: dp
  BitSelector #(.group(4)) bitselector_2 (.in(buffer_1_out), .out(bitselector_2_out), .sel(1'b1));
  BitSelector #(.group(4)) bitselector_3 (.in(buffer_1_out), .out(bitselector_3_out), .sel(1'b0));
  assign buffer_1_out = in_1;  // Buffer buffer_1, 8 bits wide
  assign buffer_1_out = multiplexer_5_out;  // Buffer buffer_2, 8 bits wide
  Demultiplexer #(.select(4), .width(8)) demultiplexer_1 (
    .out1(demultiplexer_1_out1), .out2(demultiplexer_1_out2), .out3(demultiplexer_1_out3),
    .out4(demultiplexer_1_out4), .out5(demultiplexer_1_out5), .out6(demultiplexer_1_out6),
    .out7(demultiplexer_1_out7), .out8(demultiplexer_1_out8), .out9(demultiplexer_1_out9),
    .out10(demultiplexer_1_out10), .out11(demultiplexer_1_out11), .out12(demultiplexer_1_out12),
    .out13(demultiplexer_1_out13), .out14(demultiplexer_1_out14), .out15(demultiplexer_1_out15),
    .in(buffer_1_out), .sel(in_5));  // open: out0
  Demultiplexer #(.select(4)) demultiplexer_2 (
    .out1(demultiplexer_2_out1), .out2(demultiplexer_2_out2), .out3(demultiplexer_2_out3),
    .out4(demultiplexer_2_out4), .out5(demultiplexer_2_out5), .out6(demultiplexer_2_out6),
    .out7(demultiplexer_2_out7), .out8(demultiplexer_2_out8), .out9(demultiplexer_2_out9),
    .out10(demultiplexer_2_out10), .out11(demultiplexer_2_out11), .out12(demultiplexer_2_out12),
    .out13(demultiplexer_2_out13), .out14(demultiplexer_2_out14), .out15(demultiplexer_2_out15),
    .in(bitselector_4_out), .sel(in_5));  // open: out0
  BitSelector bitselector_4 (.in(rom_1_data), .out(bitselector_4_out), .sel(3'b111));
  Register register_1 (.D(demultiplexer_1_out1), .en(demultiplexer_2_out1), .clk(in_6), .Q(register_1_q));  // open: clr
  Register register_2 (.D(demultiplexer_1_out2), .en(demultiplexer_2_out2), .clk(in_6), .Q(register_2_q));  // open: clr
  Register register_3 (.D(demultiplexer_1_out3), .en(demultiplexer_2_out3), .clk(in_6), .Q(register_3_q));  // open: clr
  Register register_4 (.D(demultiplexer_1_out4), .en(demultiplexer_2_out4), .clk(in_6), .Q(register_4_q));  // open: clr
  Register register_5 (.D(demultiplexer_1_out5), .en(demultiplexer_2_out5), .clk(in_6), .Q(register_5_q));  // open: clr
  Register register_6 (.D(demultiplexer_1_out6), .en(demultiplexer_2_out6), .clk(in_6), .Q(register_6_q));  // open: clr
  Register register_7 (.D(demultiplexer_1_out7), .en(demultiplexer_2_out7), .clk(in_6), .Q(register_7_q));  // open: clr
  Register register_8 (.D(demultiplexer_1_out8), .en(demultiplexer_2_out8), .clk(in_6), .Q(register_8_q));  // open: clr
  Register register_9 (.D(demultiplexer_1_out9), .en(demultiplexer_2_out9), .clk(in_6), .Q(register_9_q));  // open: clr
  Register register_10 (
    .D(demultiplexer_1_out10), .en(demultiplexer_2_out10), .clk(in_6), .Q(register_10_q));  // open: clr
  Register register_11 (
    .D(demultiplexer_1_out11), .en(demultiplexer_2_out11), .clk(in_6), .Q(register_11_q));  // open: clr
  Register register_12 (
    .D(demultiplexer_1_out12), .en(demultiplexer_2_out12), .clk(in_6), .Q(register_12_q));  // open: clr
  Register register_13 (
    .D(demultiplexer_1_out13), .en(demultiplexer_2_out13), .clk(in_6), .Q(register_13_q));  // open: clr
  Register register_14 (
    .D(demultiplexer_1_out14), .en(demultiplexer_2_out14), .clk(in_6), .Q(register_14_q));  // open: clr
  Register register_15 (
    .D(demultiplexer_1_out15), .en(demultiplexer_2_out15), .clk(in_6), .Q(register_15_q));  // open: clr
  Hex_Digit_Display hex_digit_display_3 (.value(bitselector_5_out));  // open: dp
  Hex_Digit_Display hex_digit_display_4 (.value(bitselector_6_out));  // open: dp
  BitSelector #(.group(4)) bitselector_5 (.in(multiplexer_1_out), .out(bitselector_5_out), .sel(1'b1));
  BitSelector #(.group(4)) bitselector_6 (.in(multiplexer_1_out), .out(bitselector_6_out), .sel(1'b0));
  Hex_Digit_Display hex_digit_display_5 (.value(bitselector_7_out));  // open: dp
  BitSelector #(.group(4)) bitselector_7 (.in(multiplexer_3_out), .out(bitselector_7_out), .sel(1'b1));
  Hex_Digit_Display hex_digit_display_6 (.value(bitselector_8_out));  // open: dp
  BitSelector #(.group(4)) bitselector_8 (.in(multiplexer_3_out), .out(bitselector_8_out), .sel(1'b0));
  Multiplexer #(.width(8)) multiplexer_1 (
    .in0(undriven), .in1(multiplexer_2_out), .out(multiplexer_1_out), .sel(bitselector_4_out));
  Multiplexer #(.select(4), .width(8)) multiplexer_2 (
    .in1(register_1_q), .in2(register_2_q), .in3(register_3_q), .in4(register_4_q), .in5(register_5_q),
    .in6(register_6_q), .in7(register_7_q), .in8(register_8_q), .in9(register_9_q), .in10(register_10_q),
    .in11(register_11_q), .in12(register_12_q), .in13(register_13_q), .in14(register_14_q),
    .in15(register_15_q), .out(multiplexer_2_out), .sel(in_3));  // open: in0
  Multiplexer #(.width(8)) multiplexer_3 (
    .in0(undriven), .in1(multiplexer_4_out), .out(multiplexer_3_out), .sel(bitselector_4_out));
  Multiplexer #(.select(4), .width(8)) multiplexer_4 (
    .in1(register_1_q), .in2(register_2_q), .in3(register_3_q), .in4(register_4_q), .in5(register_5_q),
    .in6(register_6_q), .in7(register_7_q), .in8(register_8_q), .in9(register_9_q), .in10(register_10_q),
    .in11(register_11_q), .in12(register_12_q), .in13(register_13_q), .in14(register_14_q),
    .in15(register_15_q), .out(multiplexer_4_out), .sel(in_4));  // open: in0
  Demultiplexer #(.select(3), .width(8)) demultiplexer_3 (
    .out0(demultiplexer_3_out0), .out1(demultiplexer_3_out1), .out2(demultiplexer_3_out2),
    .out3(demultiplexer_3_out3), .out4(demultiplexer_3_out4), .out5(demultiplexer_3_out5),
    .in(multiplexer_1_out), .sel(bitselector_1_out));  // open: out6, out7
  Demultiplexer #(.select(3), .width(8)) demultiplexer_4 (
    .out0(demultiplexer_4_out0), .out1(demultiplexer_4_out1), .out2(demultiplexer_4_out2),
    .out3(demultiplexer_4_out3), .out4(demultiplexer_4_out4), .in(multiplexer_3_out), .sel(bitselector_1_out));  // open: out5, out6, out7
  Adder adder_1 (.a(demultiplexer_3_out0), .b(demultiplexer_4_out0), .out(adder_1_out));  // open: cin, cout
  Subtractor subtractor_1 (
    .a(demultiplexer_3_out1), .b(demultiplexer_4_out1), .out(subtractor_1_out));  // open: bin, bout
  assign and_1_out = demultiplexer_3_out2 & demultiplexer_4_out2;  // AND_Gate and_1, 8 bits wide
  assign or_1_out = demultiplexer_3_out3 | demultiplexer_4_out3;  // OR_Gate or_1, 8 bits wide
  assign xor_1_out = demultiplexer_3_out4 ^ demultiplexer_4_out4;  // XOR_Gate xor_1, 8 bits wide
  Shifter #(.shift("lr")) shifter_1 (.in(demultiplexer_3_out5), .\dist (3'b001), .out(shifter_1_out));
  Multiplexer #(.select(3), .width(8)) multiplexer_5 (
    .in0(adder_1_out), .in1(subtractor_1_out), .in2(and_1_out), .in3(or_1_out), .in4(xor_1_out),
    .in5(shifter_1_out), .out(multiplexer_5_out), .sel(bitselector_1_out));  // open: in6, in7

  // Notes on the sheet:
  //   contents of rom_1 (hex, n*v repeats v):
  //   0 0 80 81 82 83 84 85
endmodule
