// Logisim project 8.bit_ALU.SDR.ROM.IM_0.circ as structural Verilog: 1 circuit, main circuit main
module main (
  input  in_1,
  input  in_2,
  input  [7:0] in_3
);

  wire and_1_out, bitselector_2_out, bitselector_7_out, bitselector_11_out, bitselector_13_out, clock_1_out,
       clock_2_out, demultiplexer_2_out1, demultiplexer_2_out2, demultiplexer_2_out3, demultiplexer_2_out4,
       demultiplexer_2_out5, demultiplexer_2_out6, demultiplexer_2_out7, demultiplexer_2_out8,
       demultiplexer_2_out9, demultiplexer_2_out10, demultiplexer_2_out11, demultiplexer_2_out12,
       demultiplexer_2_out13, demultiplexer_2_out14, demultiplexer_2_out15, not_1_out;
  wire [2:0] bitselector_8_out;
  wire [3:0] bitselector_1_out, bitselector_4_out, bitselector_5_out, bitselector_6_out, bitselector_9_out,
       bitselector_10_out, bitselector_12_out, bitselector_14_out, bitselector_15_out, bitselector_16_out,
       bitselector_17_out, multiplexer_1_out;
  wire [7:0] adder_2_out, and_2_out, and_3_out, bitselector_3_out, demultiplexer_1_out1,
       demultiplexer_1_out2, demultiplexer_1_out3, demultiplexer_1_out4, demultiplexer_1_out5,
       demultiplexer_1_out6, demultiplexer_1_out7, demultiplexer_1_out8, demultiplexer_1_out9,
       demultiplexer_1_out10, demultiplexer_1_out11, demultiplexer_1_out12, demultiplexer_1_out13,
       demultiplexer_1_out14, demultiplexer_1_out15, demultiplexer_3_out2, demultiplexer_3_out3,
       demultiplexer_3_out4, demultiplexer_3_out5, demultiplexer_3_out6, demultiplexer_3_out7,
       demultiplexer_4_out2, demultiplexer_4_out3, demultiplexer_4_out4, demultiplexer_4_out5,
       demultiplexer_4_out6, multiplexer_2_out, multiplexer_3_out, multiplexer_4_out, multiplexer_5_out,
       multiplexer_6_out, multiplexer_7_out, or_1_out, register_2_q, register_3_q, register_4_q,
       register_5_q, register_6_q, register_7_q, register_8_q, register_9_q, register_10_q, register_11_q,
       register_12_q, register_13_q, register_14_q, register_15_q, register_16_q, rom_2_data, shifter_1_out,
       subtractor_1_out, undriven, xor_1_out;
  wire [9:0] adder_1_out, register_1_q;
  wire [15:0] rom_1_data;

  Register #(.width(10)) register_1 (.D(adder_1_out), .en(1'b1), .clk(and_1_out), .Q(register_1_q), .clr(in_1));
  and and_1 (and_1_out, not_1_out, clock_1_out);
  not not_1 (not_1_out, bitselector_2_out);
  ROM #(.addrWidth(10), .dataWidth(16)) rom_1 (.addr(register_1_q), .data(rom_1_data));
  Adder #(.width(10)) adder_1 (.a(register_1_q), .b(10'h1), .out(adder_1_out));  // open: cin, cout
  Clock clock_1 (.out(clock_1_out));
  ROM #(.addrWidth(4)) rom_2 (.addr(bitselector_1_out), .data(rom_2_data));
  BitSelector #(.group(4), .width(16)) bitselector_1 (.in(rom_1_data), .out(bitselector_1_out), .sel(2'b11));
  assign and_2_out = rom_2_data & in_3;  // AND_Gate and_2, 8 bits wide
  BitSelector bitselector_2 (.in(and_2_out), .out(bitselector_2_out), .sel(3'b000));
  BitSelector #(.group(8), .width(16)) bitselector_3 (.in(rom_1_data), .out(bitselector_3_out), .sel(1'b0));
  BitSelector #(.group(4), .width(16)) bitselector_4 (.in(rom_1_data), .out(bitselector_4_out), .sel(2'b10));
  BitSelector #(.group(4), .width(16)) bitselector_5 (.in(rom_1_data), .out(bitselector_5_out), .sel(2'b00));
  Multiplexer #(.width(4)) multiplexer_1 (
    .in0(bitselector_5_out), .in1(bitselector_6_out), .out(multiplexer_1_out), .sel(bitselector_7_out));
  BitSelector #(.group(4), .width(16)) bitselector_6 (.in(rom_1_data), .out(bitselector_6_out), .sel(2'b10));
  BitSelector bitselector_7 (.in(rom_2_data), .out(bitselector_7_out), .sel(3'b101));
  BitSelector #(.group(3)) bitselector_8 (.in(rom_2_data), .out(bitselector_8_out), .sel(2'b00));
  Hex_Digit_Display hex_digit_display_1 (.value(bitselector_9_out));  // open: dp
  Hex_Digit_Display hex_digit_display_2 (.value(bitselector_10_out));  // open: dp
  BitSelector #(.group(4)) bitselector_9 (.in(multiplexer_2_out), .out(bitselector_9_out), .sel(1'b1));
  BitSelector #(.group(4)) bitselector_10 (.in(multiplexer_2_out), .out(bitselector_10_out), .sel(1'b0));
  Multiplexer #(.width(8)) multiplexer_2 (
    .in0(multiplexer_7_out), .in1(bitselector_3_out), .out(multiplexer_2_out), .sel(bitselector_11_out));
  BitSelector bitselector_11 (.in(rom_2_data), .out(bitselector_11_out), .sel(3'b110));
  Demultiplexer #(.select(4), .width(8)) demultiplexer_1 (
    .out1(demultiplexer_1_out1), .out2(demultiplexer_1_out2), .out3(demultiplexer_1_out3),
    .out4(demultiplexer_1_out4), .out5(demultiplexer_1_out5), .out6(demultiplexer_1_out6),
    .out7(demultiplexer_1_out7), .out8(demultiplexer_1_out8), .out9(demultiplexer_1_out9),
    .out10(demultiplexer_1_out10), .out11(demultiplexer_1_out11), .out12(demultiplexer_1_out12),
    .out13(demultiplexer_1_out13), .out14(demultiplexer_1_out14), .out15(demultiplexer_1_out15),
    .in(multiplexer_2_out), .sel(multiplexer_1_out));  // open: out0
  BitSelector #(.group(4), .width(16)) bitselector_12 (.in(rom_1_data), .out(bitselector_12_out), .sel(2'b01));
  Demultiplexer #(.select(4)) demultiplexer_2 (
    .out1(demultiplexer_2_out1), .out2(demultiplexer_2_out2), .out3(demultiplexer_2_out3),
    .out4(demultiplexer_2_out4), .out5(demultiplexer_2_out5), .out6(demultiplexer_2_out6),
    .out7(demultiplexer_2_out7), .out8(demultiplexer_2_out8), .out9(demultiplexer_2_out9),
    .out10(demultiplexer_2_out10), .out11(demultiplexer_2_out11), .out12(demultiplexer_2_out12),
    .out13(demultiplexer_2_out13), .out14(demultiplexer_2_out14), .out15(demultiplexer_2_out15),
    .in(bitselector_13_out), .sel(multiplexer_1_out));  // open: out0
  BitSelector bitselector_13 (.in(rom_2_data), .out(bitselector_13_out), .sel(3'b111));
  Clock clock_2 (.out(clock_2_out));
  Register register_2 (
    .D(demultiplexer_1_out1), .en(demultiplexer_2_out1), .clk(clock_2_out), .Q(register_2_q), .clr(in_2));
  Register register_3 (
    .D(demultiplexer_1_out2), .en(demultiplexer_2_out2), .clk(clock_2_out), .Q(register_3_q), .clr(in_2));
  Register register_4 (
    .D(demultiplexer_1_out3), .en(demultiplexer_2_out3), .clk(clock_2_out), .Q(register_4_q), .clr(in_2));
  Register register_5 (
    .D(demultiplexer_1_out4), .en(demultiplexer_2_out4), .clk(clock_2_out), .Q(register_5_q), .clr(in_2));
  Register register_6 (
    .D(demultiplexer_1_out5), .en(demultiplexer_2_out5), .clk(clock_2_out), .Q(register_6_q), .clr(in_2));
  Register register_7 (
    .D(demultiplexer_1_out6), .en(demultiplexer_2_out6), .clk(clock_2_out), .Q(register_7_q), .clr(in_2));
  Register register_8 (
    .D(demultiplexer_1_out7), .en(demultiplexer_2_out7), .clk(clock_2_out), .Q(register_8_q), .clr(in_2));
  Register register_9 (
    .D(demultiplexer_1_out8), .en(demultiplexer_2_out8), .clk(clock_2_out), .Q(register_9_q), .clr(in_2));
  Register register_10 (
    .D(demultiplexer_1_out9), .en(demultiplexer_2_out9), .clk(clock_2_out), .Q(register_10_q), .clr(in_2));
  Register register_11 (
    .D(demultiplexer_1_out10), .en(demultiplexer_2_out10), .clk(clock_2_out), .Q(register_11_q), .clr(in_2));
  Register register_12 (
    .D(demultiplexer_1_out11), .en(demultiplexer_2_out11), .clk(clock_2_out), .Q(register_12_q), .clr(in_2));
  Register register_13 (
    .D(demultiplexer_1_out12), .en(demultiplexer_2_out12), .clk(clock_2_out), .Q(register_13_q), .clr(in_2));
  Register register_14 (
    .D(demultiplexer_1_out13), .en(demultiplexer_2_out13), .clk(clock_2_out), .Q(register_14_q), .clr(in_2));
  Register register_15 (
    .D(demultiplexer_1_out14), .en(demultiplexer_2_out14), .clk(clock_2_out), .Q(register_15_q), .clr(in_2));
  Register register_16 (
    .D(demultiplexer_1_out15), .en(demultiplexer_2_out15), .clk(clock_2_out), .Q(register_16_q), .clr(in_2));
  Hex_Digit_Display hex_digit_display_3 (.value(bitselector_14_out));  // open: dp
  Hex_Digit_Display hex_digit_display_4 (.value(bitselector_15_out));  // open: dp
  BitSelector #(.group(4)) bitselector_14 (.in(multiplexer_3_out), .out(bitselector_14_out), .sel(1'b1));
  BitSelector #(.group(4)) bitselector_15 (.in(multiplexer_3_out), .out(bitselector_15_out), .sel(1'b0));
  Hex_Digit_Display hex_digit_display_5 (.value(bitselector_16_out));  // open: dp
  BitSelector #(.group(4)) bitselector_16 (.in(multiplexer_5_out), .out(bitselector_16_out), .sel(1'b1));
  Hex_Digit_Display hex_digit_display_6 (.value(bitselector_17_out));  // open: dp
  BitSelector #(.group(4)) bitselector_17 (.in(multiplexer_5_out), .out(bitselector_17_out), .sel(1'b0));
  Multiplexer #(.width(8)) multiplexer_3 (
    .in0(undriven), .in1(multiplexer_4_out), .out(multiplexer_3_out), .sel(bitselector_13_out));
  Multiplexer #(.select(4), .width(8)) multiplexer_4 (
    .in0({8{1'b0}}), .in1(register_2_q), .in2(register_3_q), .in3(register_4_q), .in4(register_5_q),
    .in5(register_6_q), .in6(register_7_q), .in7(register_8_q), .in8(register_9_q), .in9(register_10_q),
    .in10(register_11_q), .in11(register_12_q), .in12(register_13_q), .in13(register_14_q),
    .in14(register_15_q), .in15(register_16_q), .out(multiplexer_4_out), .sel(bitselector_4_out));
  Multiplexer #(.width(8)) multiplexer_5 (
    .in0(undriven), .in1(multiplexer_6_out), .out(multiplexer_5_out), .sel(bitselector_13_out));
  Multiplexer #(.select(4), .width(8)) multiplexer_6 (
    .in0({8{1'b0}}), .in1(register_2_q), .in2(register_3_q), .in3(register_4_q), .in4(register_5_q),
    .in5(register_6_q), .in6(register_7_q), .in7(register_8_q), .in8(register_9_q), .in9(register_10_q),
    .in10(register_11_q), .in11(register_12_q), .in12(register_13_q), .in13(register_14_q),
    .in14(register_15_q), .in15(register_16_q), .out(multiplexer_6_out), .sel(bitselector_12_out));
  Demultiplexer #(.select(3), .width(8)) demultiplexer_3 (
    .out2(demultiplexer_3_out2), .out3(demultiplexer_3_out3), .out4(demultiplexer_3_out4),
    .out5(demultiplexer_3_out5), .out6(demultiplexer_3_out6), .out7(demultiplexer_3_out7),
    .in(multiplexer_3_out), .sel(bitselector_8_out));  // open: out0, out1
  Demultiplexer #(.select(3), .width(8)) demultiplexer_4 (
    .out2(demultiplexer_4_out2), .out3(demultiplexer_4_out3), .out4(demultiplexer_4_out4),
    .out5(demultiplexer_4_out5), .out6(demultiplexer_4_out6), .in(multiplexer_5_out), .sel(bitselector_8_out));  // open: out0, out1, out7
  Adder adder_2 (.a(demultiplexer_3_out2), .b(demultiplexer_4_out2), .out(adder_2_out));  // open: cin, cout
  Subtractor subtractor_1 (
    .a(demultiplexer_3_out3), .b(demultiplexer_4_out3), .out(subtractor_1_out));  // open: bin, bout
  assign and_3_out = demultiplexer_3_out4 & demultiplexer_4_out4;  // AND_Gate and_3, 8 bits wide
  assign or_1_out = demultiplexer_3_out5 | demultiplexer_4_out5;  // OR_Gate or_1, 8 bits wide
  assign xor_1_out = demultiplexer_3_out6 ^ demultiplexer_4_out6;  // XOR_Gate xor_1, 8 bits wide
  Shifter #(.shift("lr")) shifter_1 (.in(demultiplexer_3_out7), .\dist (3'b001), .out(shifter_1_out));
  Multiplexer #(.select(3), .width(8)) multiplexer_7 (
    .in2(adder_2_out), .in3(subtractor_1_out), .in4(and_3_out), .in5(or_1_out), .in6(xor_1_out),
    .in7(shifter_1_out), .out(multiplexer_7_out), .sel(bitselector_8_out));  // open: in0, in1

  // Notes on the sheet:
  //   contents of rom_2 (hex, n*v repeats v):
  //   0 1 82 83 84 85 86 87 e0
endmodule
