// Logisim project 8.bit_SDR_0.circ as structural Verilog: 1 circuit, main circuit main
module main (
  input  [7:0] in_1,
  input  [7:0] in_2,
  input  in_3,
  input  [7:0] in_4,
  input  [7:0] in_5,
  input  [3:0] in_6,
  input  in_7,
  input  in_8,
  input  [3:0] in_9,
  input  in_10,
  input  [3:0] in_11
);

  wire demultiplexer_2_out1, demultiplexer_2_out2, demultiplexer_2_out3, demultiplexer_2_out4,
       demultiplexer_2_out5, demultiplexer_2_out6, demultiplexer_2_out7, demultiplexer_2_out8,
       demultiplexer_2_out9, demultiplexer_2_out10, demultiplexer_2_out11, demultiplexer_2_out12,
       demultiplexer_2_out13, demultiplexer_2_out14, demultiplexer_2_out15;
  wire [3:0] bitselector_1_out, bitselector_2_out, bitselector_3_out, bitselector_4_out;
  wire [7:0] demultiplexer_1_out1, demultiplexer_1_out2, demultiplexer_1_out3, demultiplexer_1_out4,
       demultiplexer_1_out5, demultiplexer_1_out6, demultiplexer_1_out7, demultiplexer_1_out8,
       demultiplexer_1_out9, demultiplexer_1_out10, demultiplexer_1_out11, demultiplexer_1_out12,
       demultiplexer_1_out13, demultiplexer_1_out14, demultiplexer_1_out15, multiplexer_1_out,
       multiplexer_2_out, multiplexer_3_out, multiplexer_4_out, register_1_q, register_2_q, register_3_q,
       register_4_q, register_5_q, register_6_q, register_7_q, register_8_q, register_9_q, register_10_q,
       register_11_q, register_12_q, register_13_q, register_14_q, register_15_q;

  Demultiplexer #(.select(4), .width(8)) demultiplexer_1 (
    .out1(demultiplexer_1_out1), .out2(demultiplexer_1_out2), .out3(demultiplexer_1_out3),
    .out4(demultiplexer_1_out4), .out5(demultiplexer_1_out5), .out6(demultiplexer_1_out6),
    .out7(demultiplexer_1_out7), .out8(demultiplexer_1_out8), .out9(demultiplexer_1_out9),
    .out10(demultiplexer_1_out10), .out11(demultiplexer_1_out11), .out12(demultiplexer_1_out12),
    .out13(demultiplexer_1_out13), .out14(demultiplexer_1_out14), .out15(demultiplexer_1_out15), .in(in_4),
    .sel(in_6));  // open: out0
  Demultiplexer #(.select(4)) demultiplexer_2 (
    .out1(demultiplexer_2_out1), .out2(demultiplexer_2_out2), .out3(demultiplexer_2_out3),
    .out4(demultiplexer_2_out4), .out5(demultiplexer_2_out5), .out6(demultiplexer_2_out6),
    .out7(demultiplexer_2_out7), .out8(demultiplexer_2_out8), .out9(demultiplexer_2_out9),
    .out10(demultiplexer_2_out10), .out11(demultiplexer_2_out11), .out12(demultiplexer_2_out12),
    .out13(demultiplexer_2_out13), .out14(demultiplexer_2_out14), .out15(demultiplexer_2_out15), .in(in_7),
    .sel(in_6));  // open: out0
  Register register_1 (.D(demultiplexer_1_out1), .en(demultiplexer_2_out1), .clk(in_8), .Q(register_1_q));  // open: clr
  Register register_2 (.D(demultiplexer_1_out2), .en(demultiplexer_2_out2), .clk(in_8), .Q(register_2_q));  // open: clr
  Register register_3 (.D(demultiplexer_1_out3), .en(demultiplexer_2_out3), .clk(in_8), .Q(register_3_q));  // open: clr
  Register register_4 (.D(demultiplexer_1_out4), .en(demultiplexer_2_out4), .clk(in_8), .Q(register_4_q));  // open: clr
  Register register_5 (.D(demultiplexer_1_out5), .en(demultiplexer_2_out5), .clk(in_8), .Q(register_5_q));  // open: clr
  Register register_6 (.D(demultiplexer_1_out6), .en(demultiplexer_2_out6), .clk(in_8), .Q(register_6_q));  // open: clr
  Register register_7 (.D(demultiplexer_1_out7), .en(demultiplexer_2_out7), .clk(in_8), .Q(register_7_q));  // open: clr
  Register register_8 (.D(demultiplexer_1_out8), .en(demultiplexer_2_out8), .clk(in_8), .Q(register_8_q));  // open: clr
  Register register_9 (.D(demultiplexer_1_out9), .en(demultiplexer_2_out9), .clk(in_8), .Q(register_9_q));  // open: clr
  Register register_10 (
    .D(demultiplexer_1_out10), .en(demultiplexer_2_out10), .clk(in_8), .Q(register_10_q));  // open: clr
  Register register_11 (
    .D(demultiplexer_1_out11), .en(demultiplexer_2_out11), .clk(in_8), .Q(register_11_q));  // open: clr
  Register register_12 (
    .D(demultiplexer_1_out12), .en(demultiplexer_2_out12), .clk(in_8), .Q(register_12_q));  // open: clr
  Register register_13 (
    .D(demultiplexer_1_out13), .en(demultiplexer_2_out13), .clk(in_8), .Q(register_13_q));  // open: clr
  Register register_14 (
    .D(demultiplexer_1_out14), .en(demultiplexer_2_out14), .clk(in_8), .Q(register_14_q));  // open: clr
  Register register_15 (
    .D(demultiplexer_1_out15), .en(demultiplexer_2_out15), .clk(in_8), .Q(register_15_q));  // open: clr
  Multiplexer #(.width(8)) multiplexer_1 (.in0(in_1), .in1(multiplexer_2_out), .out(multiplexer_1_out), .sel(in_7));
  Multiplexer #(.select(4), .width(8)) multiplexer_2 (
    .in0(in_2), .in1(register_1_q), .in2(register_2_q), .in3(register_3_q), .in4(register_4_q),
    .in5(register_5_q), .in6(register_6_q), .in7(register_7_q), .in8(register_8_q), .in9(register_9_q),
    .in10(register_10_q), .in11(register_11_q), .in12(register_12_q), .in13(register_13_q),
    .in14(register_14_q), .in15(register_15_q), .out(multiplexer_2_out), .sel(in_9));
  Multiplexer #(.width(8)) multiplexer_3 (.in0(in_5), .in1(multiplexer_4_out), .out(multiplexer_3_out), .sel(in_7));
  Multiplexer #(.select(4), .width(8)) multiplexer_4 (
    .in0(in_2), .in1(register_1_q), .in2(register_2_q), .in3(register_3_q), .in4(register_4_q),
    .in5(register_5_q), .in6(register_6_q), .in7(register_7_q), .in8(register_8_q), .in9(register_9_q),
    .in10(register_10_q), .in11(register_11_q), .in12(register_12_q), .in13(register_13_q),
    .in14(register_14_q), .in15(register_15_q), .out(multiplexer_4_out), .sel(in_11));
  Hex_Digit_Display hex_digit_display_1 (.value(bitselector_1_out));  // open: dp
  BitSelector #(.group(4)) bitselector_1 (.in(multiplexer_1_out), .out(bitselector_1_out), .sel(in_3));
  Hex_Digit_Display hex_digit_display_2 (.value(bitselector_2_out));  // open: dp
  BitSelector #(.group(4)) bitselector_2 (.in(multiplexer_3_out), .out(bitselector_2_out), .sel(in_10));
  Hex_Digit_Display hex_digit_display_3 (.value(bitselector_3_out));  // open: dp
  BitSelector #(.group(4)) bitselector_3 (.in(multiplexer_1_out), .out(bitselector_3_out), .sel(1'b1));
  Hex_Digit_Display hex_digit_display_4 (.value(bitselector_4_out));  // open: dp
  BitSelector #(.group(4)) bitselector_4 (.in(multiplexer_3_out), .out(bitselector_4_out), .sel(1'b1));
endmodule
