// Logisim project l_16_bit_computer.circ as structural Verilog: 8 circuits, main circuit main
module main (
);

  wire alu_1_borrow_out, alu_1_carry_out, alu_1_equals_flag, alu_1_grater_flag, alu_1_less_flag,
       alu_1_zero_flag, clk_1_clock_out, clock_1_out, undriven, undriven_2, undriven_3, undriven_4;
  wire [6:0] pull_resistor_16_node;
  wire [15:0] accumlator_1_always_out, b_register_1_always_out, program_counter_1_always_out;
  wire [15:7] pull_resistor_9_node;

  Clock clock_1 (.out(clock_1_out));
  CLK clk_1 (.CLOCK_IN(clock_1_out), .CLOCK_OUT(clk_1_clock_out));  // open: CLOCK_ENABLE, MANUAL_TICK, HALT
  LED led_1 (.in(pull_resistor_9_node[15]));
  LED led_2 (.in(pull_resistor_9_node[14]));
  Pull_Resistor pull_resistor_1 (.node(pull_resistor_9_node[15]));
  Pull_Resistor pull_resistor_2 (.node(pull_resistor_9_node[14]));
  LED led_3 (.in(pull_resistor_9_node[13]));
  LED led_4 (.in(pull_resistor_9_node[12]));
  LED led_5 (.in(pull_resistor_9_node[11]));
  LED led_6 (.in(pull_resistor_9_node[10]));
  Pull_Resistor pull_resistor_3 (.node(pull_resistor_9_node[13]));
  Pull_Resistor pull_resistor_4 (.node(pull_resistor_9_node[12]));
  Pull_Resistor pull_resistor_5 (.node(pull_resistor_9_node[11]));
  Pull_Resistor pull_resistor_6 (.node(pull_resistor_9_node[10]));
  LED led_7 (.in(pull_resistor_9_node[9]));
  LED led_8 (.in(pull_resistor_9_node[8]));
  LED led_9 (.in(pull_resistor_9_node[7]));
  LED led_10 (.in(pull_resistor_16_node[6]));
  Pull_Resistor pull_resistor_7 (.node(pull_resistor_9_node[9]));
  Pull_Resistor pull_resistor_8 (.node(pull_resistor_9_node[8]));
  Pull_Resistor pull_resistor_9 (.node(pull_resistor_9_node[7]));
  Pull_Resistor pull_resistor_10 (.node(pull_resistor_16_node[6]));
  LED led_11 (.in(pull_resistor_16_node[5]));
  LED led_12 (.in(pull_resistor_16_node[4]));
  LED led_13 (.in(pull_resistor_16_node[3]));
  LED led_14 (.in(pull_resistor_16_node[2]));
  Pull_Resistor pull_resistor_11 (.node(pull_resistor_16_node[5]));
  Pull_Resistor pull_resistor_12 (.node(pull_resistor_16_node[4]));
  Pull_Resistor pull_resistor_13 (.node(pull_resistor_16_node[3]));
  Pull_Resistor pull_resistor_14 (.node(pull_resistor_16_node[2]));
  LED led_15 (.in(pull_resistor_16_node[1]));
  LED led_16 (.in(pull_resistor_16_node[0]));
  Pull_Resistor pull_resistor_15 (.node(pull_resistor_16_node[1]));
  Pull_Resistor pull_resistor_16 (.node(pull_resistor_16_node[0]));
  TTY tty_1 (.data(pull_resistor_16_node));  // open: clk, we, clr
  LED led_17 (.in(program_counter_1_always_out[15]));
  LED led_18 (.in(program_counter_1_always_out[14]));
  LED led_19 (.in(program_counter_1_always_out[13]));
  LED led_20 (.in(program_counter_1_always_out[12]));
  LED led_21 (.in(program_counter_1_always_out[11]));
  LED led_22 (.in(program_counter_1_always_out[10]));
  LED led_23 (.in(program_counter_1_always_out[9]));
  LED led_24 (.in(program_counter_1_always_out[8]));
  LED led_25 (.in(program_counter_1_always_out[7]));
  LED led_26 (.in(program_counter_1_always_out[6]));
  LED led_27 (.in(program_counter_1_always_out[5]));
  LED led_28 (.in(program_counter_1_always_out[4]));
  PROGRAM_COUNTER program_counter_1 (
    .RESET(undriven), .JUMP(undriven_2), .COUNTER_ENABLE(undriven_3), .CLOCK(clk_1_clock_out),
    .ADDRESS_IN({pull_resistor_9_node, pull_resistor_16_node}), .COUNTER_OUT(undriven_4),
    .ALWAYS_OUT(program_counter_1_always_out), .ADDRESS_OUT({pull_resistor_9_node, pull_resistor_16_node}));
  ACCUMLATOR accumlator_1 (
    .DATA_IN({pull_resistor_9_node, pull_resistor_16_node}), .CLOCK(clk_1_clock_out),
    .ALWAYS_OUT(accumlator_1_always_out));  // open: A_WRITE, A_READ, RESET, DATA_OUT
  ALU alu_1 (
    .A_IN(accumlator_1_always_out), .B_IN(b_register_1_always_out),
    .DATA_OUT({pull_resistor_9_node, pull_resistor_16_node}), .CARRY_OUT(alu_1_carry_out),
    .BORROW_OUT(alu_1_borrow_out), .GRATER_FLAG(alu_1_grater_flag), .EQUALS_FLAG(alu_1_equals_flag),
    .LESS_FLAG(alu_1_less_flag), .ZERO_FLAG(alu_1_zero_flag));  // open: CARRY_IN, BORROW_IN, ADD, SUB, NOT_A, A_AND_B, A_OR_B, A_XOR_B, A_NAND_B, A_NOR_B
  B_REGISTER b_register_1 (
    .DATA_IN({pull_resistor_9_node, pull_resistor_16_node}), .CLOCK(clk_1_clock_out),
    .ALWAYS_OUT(b_register_1_always_out), .DATA_OUT({pull_resistor_9_node, pull_resistor_16_node}));  // open: B_WRITE, B_READ, RESET
  Y_AND_Y_REGISTER y_and_y_register_1 (
    .DATA_IN({pull_resistor_9_node, pull_resistor_16_node}), .CLOCK(clk_1_clock_out),
    .DATA_OUT({pull_resistor_9_node, pull_resistor_16_node}));  // open: WRITE_X, WRITE_Y, READ_X, READ_Y, RESET, X_ALL_OUT, Y_ALL_OUT
  LED led_29 (.in(program_counter_1_always_out[3]));
  LED led_30 (.in(program_counter_1_always_out[2]));
  LED led_31 (.in(program_counter_1_always_out[1]));
  LED led_32 (.in(program_counter_1_always_out[0]));
  FLAGS_REGISTER flags_register_1 (
    .CARRY(alu_1_carry_out), .BORROW(alu_1_borrow_out), .GRATER(alu_1_grater_flag),
    .EQUALS(alu_1_equals_flag), .LESS(alu_1_less_flag), .ZERO(alu_1_zero_flag), .CLOCK(clk_1_clock_out));  // open: MATH_FLAGS_SET, COMPARE_FLAGS_SET, RESET, CARRY_FLAG, BORROW_FLAG, GRATER_FLAG, EQUALS_FLAG, LESS_FLAG, ZERO_FLAG
endmodule

module CLK (
  input  CLOCK_IN,
  input  CLOCK_ENABLE,
  input  MANUAL_TICK,
  input  HALT,
  output CLOCK_OUT
);

  wire and_1_out, and_2_out, not_1_out, not_2_out, or_1_out;

  and and_1 (and_1_out, CLOCK_IN, CLOCK_ENABLE);
  not not_1 (not_1_out, CLOCK_ENABLE);
  not not_2 (not_2_out, HALT);
  and and_2 (and_2_out, not_1_out, MANUAL_TICK);
  or or_1 (or_1_out, and_1_out, and_2_out);
  and and_3 (CLOCK_OUT, or_1_out, not_2_out);
endmodule

module PROGRAM_COUNTER (
  input  RESET,
  input  JUMP,
  input  COUNTER_ENABLE,
  input  CLOCK,
  input  [15:0] ADDRESS_IN,
  input  COUNTER_OUT,
  output [15:0] ALWAYS_OUT,
  output [15:0] ADDRESS_OUT
);

  Counter #(.max('hffff), .width(16)) counter_1 (
    .clr(RESET), .load(JUMP), .up(COUNTER_ENABLE), .count(COUNTER_ENABLE), .clk(CLOCK), .D(ADDRESS_IN),
    .Q(ALWAYS_OUT));  // open: carry
  assign ADDRESS_OUT = COUNTER_OUT ? ALWAYS_OUT : 16'bz;  // Controlled_Buffer controlled_buffer_1
endmodule

module ACCUMLATOR (
  input  [15:0] DATA_IN,
  input  A_WRITE,
  input  A_READ,
  input  CLOCK,
  input  RESET,
  output [15:0] ALWAYS_OUT,
  output [15:0] DATA_OUT
);

  Register #(.width(16)) register_1 (.D(DATA_IN), .en(A_WRITE), .clk(CLOCK), .Q(ALWAYS_OUT), .clr(RESET));
  assign DATA_OUT = A_READ ? ALWAYS_OUT : 16'bz;  // Controlled_Buffer controlled_buffer_1
endmodule

module ALU (
  input  CARRY_IN,
  input  BORROW_IN,
  input  [15:0] A_IN,
  input  [15:0] B_IN,
  input  ADD,
  input  SUB,
  input  NOT_A,
  input  A_AND_B,
  input  A_OR_B,
  input  A_XOR_B,
  input  A_NAND_B,
  input  A_NOR_B,
  output [15:0] DATA_OUT,
  output CARRY_OUT,
  output BORROW_OUT,
  output GRATER_FLAG,
  output EQUALS_FLAG,
  output LESS_FLAG,
  output ZERO_FLAG
);

  wire or_2_out, or_3_out, or_4_out, or_5_out, or_6_out, or_7_out, or_8_out, or_9_out, or_10_out, or_11_out,
       or_12_out, or_13_out, or_14_out, or_15_out, or_16_out;
  wire [15:0] adder_1_out, and_1_out, nand_1_out, nor_1_out, not_1_out, or_1_out, subtractor_1_out, xor_1_out;

  Adder #(.width(16)) adder_1 (.a(A_IN), .b(B_IN), .out(adder_1_out), .cin(CARRY_IN), .cout(CARRY_OUT));
  Subtractor #(.width(16)) subtractor_1 (
    .a(A_IN), .b(B_IN), .out(subtractor_1_out), .bin(BORROW_IN), .bout(BORROW_OUT));
  Comparator #(.width(16)) comparator_1 (.a(A_IN), .b(B_IN), .gt(GRATER_FLAG), .eq(EQUALS_FLAG), .lt(LESS_FLAG));
  assign not_1_out = ~A_IN;  // NOT_Gate not_1, 16 bits wide
  assign and_1_out = A_IN & B_IN;  // AND_Gate and_1, 16 bits wide
  assign or_1_out = A_IN | B_IN;  // OR_Gate or_1, 16 bits wide
  assign xor_1_out = A_IN ^ B_IN;  // XOR_Gate xor_1, 16 bits wide
  assign nand_1_out = ~(A_IN & B_IN);  // NAND_Gate nand_1, 16 bits wide
  assign nor_1_out = ~(A_IN | B_IN);  // NOR_Gate nor_1, 16 bits wide
  assign DATA_OUT = ADD ? adder_1_out : 16'bz;  // Controlled_Buffer controlled_buffer_1
  assign DATA_OUT = SUB ? subtractor_1_out : 16'bz;  // Controlled_Buffer controlled_buffer_2
  assign DATA_OUT = NOT_A ? not_1_out : 16'bz;  // Controlled_Buffer controlled_buffer_3
  assign DATA_OUT = A_AND_B ? and_1_out : 16'bz;  // Controlled_Buffer controlled_buffer_4
  assign DATA_OUT = A_OR_B ? or_1_out : 16'bz;  // Controlled_Buffer controlled_buffer_5
  assign DATA_OUT = A_XOR_B ? xor_1_out : 16'bz;  // Controlled_Buffer controlled_buffer_6
  assign DATA_OUT = A_NAND_B ? nand_1_out : 16'bz;  // Controlled_Buffer controlled_buffer_7
  assign DATA_OUT = A_NOR_B ? nor_1_out : 16'bz;  // Controlled_Buffer controlled_buffer_8
  or or_2 (or_2_out, DATA_OUT[0], DATA_OUT[1]);
  or or_3 (or_3_out, or_2_out, DATA_OUT[2]);
  or or_4 (or_4_out, or_3_out, DATA_OUT[3]);
  or or_5 (or_5_out, or_4_out, DATA_OUT[4]);
  or or_6 (or_6_out, or_5_out, DATA_OUT[5]);
  or or_7 (or_7_out, or_6_out, DATA_OUT[6]);
  or or_8 (or_8_out, or_7_out, DATA_OUT[7]);
  or or_9 (or_9_out, or_8_out, DATA_OUT[8]);
  or or_10 (or_10_out, or_9_out, DATA_OUT[9]);
  or or_11 (or_11_out, or_10_out, DATA_OUT[10]);
  or or_12 (or_12_out, or_11_out, DATA_OUT[11]);
  or or_13 (or_13_out, or_12_out, DATA_OUT[12]);
  or or_14 (or_14_out, or_13_out, DATA_OUT[13]);
  or or_15 (or_15_out, or_14_out, DATA_OUT[14]);
  or or_16 (or_16_out, or_15_out, DATA_OUT[15]);
  not not_2 (ZERO_FLAG, or_16_out);
  Pull_Resistor pull_resistor_1 (.node(DATA_OUT[0]));
  Pull_Resistor pull_resistor_2 (.node(DATA_OUT[1]));
  Pull_Resistor pull_resistor_3 (.node(DATA_OUT[2]));
  Pull_Resistor pull_resistor_4 (.node(DATA_OUT[3]));
  Pull_Resistor pull_resistor_5 (.node(DATA_OUT[4]));
  Pull_Resistor pull_resistor_6 (.node(DATA_OUT[5]));
  Pull_Resistor pull_resistor_7 (.node(DATA_OUT[6]));
  Pull_Resistor pull_resistor_8 (.node(DATA_OUT[7]));
  Pull_Resistor pull_resistor_9 (.node(DATA_OUT[8]));
  Pull_Resistor pull_resistor_10 (.node(DATA_OUT[9]));
  Pull_Resistor pull_resistor_11 (.node(DATA_OUT[10]));
  Pull_Resistor pull_resistor_12 (.node(DATA_OUT[11]));
  Pull_Resistor pull_resistor_13 (.node(DATA_OUT[12]));
  Pull_Resistor pull_resistor_14 (.node(DATA_OUT[13]));
  Pull_Resistor pull_resistor_15 (.node(DATA_OUT[14]));
  Pull_Resistor pull_resistor_16 (.node(DATA_OUT[15]));
endmodule

module FLAGS_REGISTER (
  input  CARRY,
  input  BORROW,
  input  GRATER,
  input  EQUALS,
  input  LESS,
  input  ZERO,
  input  MATH_FLAGS_SET,
  input  COMPARE_FLAGS_SET,
  input  CLOCK,
  input  RESET,
  output CARRY_FLAG,
  output BORROW_FLAG,
  output GRATER_FLAG,
  output EQUALS_FLAG,
  output LESS_FLAG,
  output ZERO_FLAG
);

  Register #(.width(1)) register_1 (.D(CARRY), .en(MATH_FLAGS_SET), .clk(CLOCK), .Q(CARRY_FLAG), .clr(RESET));
  Register #(.width(1)) register_2 (.D(BORROW), .en(MATH_FLAGS_SET), .clk(CLOCK), .Q(BORROW_FLAG), .clr(RESET));
  Register #(.width(1)) register_3 (.D(GRATER), .en(COMPARE_FLAGS_SET), .clk(CLOCK), .Q(GRATER_FLAG), .clr(RESET));
  Register #(.width(1)) register_4 (.D(EQUALS), .en(COMPARE_FLAGS_SET), .clk(CLOCK), .Q(EQUALS_FLAG), .clr(RESET));
  Register #(.width(1)) register_5 (.D(LESS), .en(COMPARE_FLAGS_SET), .clk(CLOCK), .Q(LESS_FLAG), .clr(RESET));
  Register #(.width(1)) register_6 (.D(ZERO), .en(MATH_FLAGS_SET), .clk(CLOCK), .Q(ZERO_FLAG), .clr(RESET));
endmodule

module B_REGISTER (
  input  [15:0] DATA_IN,
  input  B_WRITE,
  input  B_READ,
  input  CLOCK,
  input  RESET,
  output [15:0] ALWAYS_OUT,
  output [15:0] DATA_OUT
);

  Register #(.width(16)) register_1 (.D(DATA_IN), .en(B_WRITE), .clk(CLOCK), .Q(ALWAYS_OUT), .clr(RESET));
  assign DATA_OUT = B_READ ? ALWAYS_OUT : 16'bz;  // Controlled_Buffer controlled_buffer_1
endmodule

module Y_AND_Y_REGISTER (
  input  [15:0] DATA_IN,
  input  WRITE_X,
  input  WRITE_Y,
  input  READ_X,
  input  READ_Y,
  input  CLOCK,
  input  RESET,
  output [15:0] X_ALL_OUT,
  output [15:0] DATA_OUT,
  output [15:0] Y_ALL_OUT
);

  Register #(.width(16)) X (.D(DATA_IN), .en(WRITE_X), .clk(CLOCK), .Q(X_ALL_OUT), .clr(RESET));
  Register #(.width(16)) Y (.D(DATA_IN), .en(WRITE_Y), .clk(CLOCK), .Q(Y_ALL_OUT), .clr(RESET));
  assign DATA_OUT = READ_X ? X_ALL_OUT : 16'bz;  // Controlled_Buffer controlled_buffer_1
  assign DATA_OUT = READ_Y ? Y_ALL_OUT : 16'bz;  // Controlled_Buffer controlled_buffer_2
endmodule
