// Logisim project l_8.bit_SDR.ALU.ROM.IM.PC.CS.DM.circ as structural Verilog: 1 circuit, main circuit main
module main (
  input  in_1
);

  wire adder_2_cout, and_1_out, and_2_out, bitselector_15_out, bitselector_16_out, bitselector_17_out,
       bitselector_18_out, bitselector_20_out, bitselector_21_out, bitselector_22_out, bitselector_23_out,
       clock_1_out, d_ff_1_q, d_ff_1_qn, d_ff_2_q, d_ff_2_qn, demultiplexer_1_out1, demultiplexer_1_out2,
       demultiplexer_1_out3, demultiplexer_1_out4, demultiplexer_1_out5, demultiplexer_1_out6,
       demultiplexer_1_out7, demultiplexer_1_out8, demultiplexer_1_out9, demultiplexer_1_out10,
       demultiplexer_1_out11, demultiplexer_1_out12, demultiplexer_1_out13, demultiplexer_1_out14,
       demultiplexer_1_out15, multiplexer_1_out, multiplexer_2_out, multiplexer_3_out, multiplexer_4_out,
       multiplexer_5_out, multiplexer_8_out, multiplexer_10_out, multiplexer_11_out, multiplexer_12_out,
       multiplexer_19_out, multiplexer_20_out, multiplexer_21_out, multiplexer_22_out, multiplexer_23_out,
       multiplexer_26_out, multiplexer_30_out, multiplexer_31_out, multiplexer_34_out, multiplexer_35_out,
       multiplexer_36_out, multiplexer_37_out, not_1_out, not_2_out, not_3_out, not_4_out, not_5_out,
       or_2_out, or_5_out, subtractor_1_bout;
  wire [1:0] bitselector_3_out, bitselector_19_out, multiplexer_6_out, multiplexer_7_out, multiplexer_14_out,
       multiplexer_33_out, or_1_out;
  wire [2:0] bitselector_12_out, bitselector_13_out, bitselector_14_out, or_3_out, or_4_out, shifter_2_out,
       shifter_3_out;
  wire [3:0] bitselector_1_out, bitselector_5_out, bitselector_7_out, bitselector_8_out, bitselector_9_out,
       bitselector_10_out, bitselector_11_out, multiplexer_13_out, multiplexer_18_out;
  wire [7:0] adder_2_out, and_3_out, bitselector_4_out, bitselector_6_out, multiplexer_15_out,
       multiplexer_16_out, multiplexer_17_out, multiplexer_24_out, multiplexer_25_out, multiplexer_27_out,
       multiplexer_28_out, multiplexer_29_out, multiplexer_32_out, nor_1_out, ram_1_dout, register_18_q,
       register_19_q, register_20_q, register_21_q, register_22_q, register_23_q, register_24_q,
       register_25_q, register_26_q, register_27_q, register_28_q, register_29_q, register_30_q,
       register_31_q, register_32_q, shifter_1_out, subtractor_1_out, xor_1_out;
  wire [9:0] adder_1_out, bitselector_2_out, controlled_buffer_1_out, controlled_buffer_2_out,
       controlled_buffer_3_out, controlled_buffer_5_out, controlled_buffer_9_out, controlled_buffer_10_out,
       controlled_buffer_11_out, controlled_buffer_13_out, controlled_buffer_15_out,
       controlled_buffer_17_out, controlled_buffer_19_out, controlled_buffer_21_out,
       controlled_buffer_25_out, controlled_buffer_26_out, controlled_buffer_27_out,
       controlled_buffer_29_out, multiplexer_9_out, register_1_q, register_2_q, register_3_q, register_4_q,
       register_5_q, register_6_q, register_7_q, register_8_q, register_9_q, register_10_q, register_11_q,
       register_12_q, register_13_q, register_14_q, register_16_q, register_17_q;
  wire [15:0] rom_1_data;

  not not_1 (not_1_out, not_2_out);
  not not_2 (not_2_out, multiplexer_22_out);
  not not_3 (not_3_out, not_2_out);
  BitSelector #(.group(4), .width(16)) bitselector_1 (.in(rom_1_data), .out(bitselector_1_out), .sel(2'b11));
  Register #(.width(10)) register_1 (
    .D(controlled_buffer_1_out), .en(multiplexer_21_out), .clk(and_2_out), .Q(register_1_q), .clr(in_1));
  assign controlled_buffer_1_out = not_2_out ? adder_1_out : 10'bz;  // Controlled_Buffer controlled_buffer_1
  assign controlled_buffer_2_out = not_2_out ? controlled_buffer_1_out : 10'bz;  // Controlled_Buffer controlled_buffer_2
  Register #(.width(10)) register_2 (
    .D(controlled_buffer_2_out), .en(multiplexer_21_out), .clk(and_2_out), .Q(register_2_q), .clr(in_1));
  Multiplexer #(.select(4)) multiplexer_1 (
    .in0(1'b0), .in1(1'b0), .in2(1'b0), .in3(1'b1), .in4(1'b0), .in5(1'b1), .in6(1'b0), .in7(1'b1),
    .in8(1'b0), .in9(1'b0), .in10(1'b0), .in11(1'b0), .in12(1'b0), .in13(1'b0), .in14(1'b0), .in15(1'b0),
    .out(multiplexer_1_out), .sel(bitselector_1_out));
  assign controlled_buffer_3_out = not_2_out ? register_1_q : 10'bz;  // Controlled_Buffer controlled_buffer_3
  assign controlled_buffer_1_out = not_1_out ? controlled_buffer_2_out : 10'bz;  // Controlled_Buffer controlled_buffer_4
  assign controlled_buffer_5_out = not_2_out ? controlled_buffer_3_out : 10'bz;  // Controlled_Buffer controlled_buffer_5
  assign controlled_buffer_2_out = not_3_out ? register_3_q : 10'bz;  // Controlled_Buffer controlled_buffer_6
  Register #(.width(10)) register_3 (
    .D(controlled_buffer_5_out), .en(multiplexer_21_out), .clk(and_2_out), .Q(register_3_q), .clr(in_1));
  Register #(.width(10)) register_4 (
    .D(controlled_buffer_3_out), .en(multiplexer_21_out), .clk(and_2_out), .Q(register_4_q), .clr(in_1));
  assign controlled_buffer_3_out = not_1_out ? controlled_buffer_5_out : 10'bz;  // Controlled_Buffer controlled_buffer_7
  assign controlled_buffer_5_out = not_3_out ? register_6_q : 10'bz;  // Controlled_Buffer controlled_buffer_8
  Multiplexer #(.select(4)) multiplexer_2 (
    .in0(1'b0), .in1(1'b0), .in2(1'b0), .in3(1'b0), .in4(1'b1), .in5(1'b1), .in6(1'b0), .in7(1'b0),
    .in8(1'b0), .in9(1'b0), .in10(1'b0), .in11(1'b0), .in12(1'b0), .in13(1'b0), .in14(1'b0), .in15(1'b0),
    .out(multiplexer_2_out), .sel(bitselector_1_out));
  Register #(.width(10)) register_5 (
    .D(controlled_buffer_9_out), .en(multiplexer_21_out), .clk(and_2_out), .Q(register_5_q), .clr(in_1));
  assign controlled_buffer_9_out = not_2_out ? register_4_q : 10'bz;  // Controlled_Buffer controlled_buffer_9
  assign controlled_buffer_10_out = not_2_out ? controlled_buffer_9_out : 10'bz;  // Controlled_Buffer controlled_buffer_10
  Register #(.width(10)) register_6 (
    .D(controlled_buffer_10_out), .en(multiplexer_21_out), .clk(and_2_out), .Q(register_6_q), .clr(in_1));
  Register #(.width(10)) register_7 (
    .D(controlled_buffer_11_out), .en(multiplexer_21_out), .clk(and_2_out), .Q(register_7_q), .clr(in_1));
  assign controlled_buffer_11_out = not_2_out ? register_5_q : 10'bz;  // Controlled_Buffer controlled_buffer_11
  assign controlled_buffer_9_out = not_1_out ? controlled_buffer_10_out : 10'bz;  // Controlled_Buffer controlled_buffer_12
  assign controlled_buffer_13_out = not_2_out ? controlled_buffer_11_out : 10'bz;  // Controlled_Buffer controlled_buffer_13
  assign controlled_buffer_10_out = not_3_out ? register_8_q : 10'bz;  // Controlled_Buffer controlled_buffer_14
  Register #(.width(10)) register_8 (
    .D(controlled_buffer_13_out), .en(multiplexer_21_out), .clk(and_2_out), .Q(register_8_q), .clr(in_1));
  Register #(.width(10)) register_9 (
    .D(controlled_buffer_15_out), .en(multiplexer_21_out), .clk(and_2_out), .Q(register_9_q), .clr(in_1));
  assign controlled_buffer_15_out = not_2_out ? register_7_q : 10'bz;  // Controlled_Buffer controlled_buffer_15
  assign controlled_buffer_11_out = not_1_out ? controlled_buffer_13_out : 10'bz;  // Controlled_Buffer controlled_buffer_16
  assign controlled_buffer_17_out = not_2_out ? controlled_buffer_15_out : 10'bz;  // Controlled_Buffer controlled_buffer_17
  assign controlled_buffer_13_out = not_3_out ? register_10_q : 10'bz;  // Controlled_Buffer controlled_buffer_18
  Register #(.width(10)) register_10 (
    .D(controlled_buffer_17_out), .en(multiplexer_21_out), .clk(and_2_out), .Q(register_10_q), .clr(in_1));
  Multiplexer #(.select(4)) multiplexer_3 (
    .in0(1'b0), .in1(1'b0), .in2(1'b0), .in3(1'b0), .in4(1'b0), .in5(1'b0), .in6(1'b1), .in7(1'b1),
    .in8(1'b0), .in9(1'b0), .in10(1'b0), .in11(1'b0), .in12(1'b0), .in13(1'b0), .in14(1'b0), .in15(1'b0),
    .out(multiplexer_3_out), .sel(bitselector_1_out));
  assign controlled_buffer_19_out = not_2_out ? register_9_q : 10'bz;  // Controlled_Buffer controlled_buffer_19
  assign controlled_buffer_15_out = not_1_out ? controlled_buffer_17_out : 10'bz;  // Controlled_Buffer controlled_buffer_20
  assign controlled_buffer_21_out = not_2_out ? controlled_buffer_19_out : 10'bz;  // Controlled_Buffer controlled_buffer_21
  assign controlled_buffer_17_out = not_3_out ? register_11_q : 10'bz;  // Controlled_Buffer controlled_buffer_22
  Register #(.width(10)) register_11 (
    .D(controlled_buffer_21_out), .en(multiplexer_21_out), .clk(and_2_out), .Q(register_11_q), .clr(in_1));
  Register #(.width(10)) register_12 (
    .D(controlled_buffer_19_out), .en(multiplexer_21_out), .clk(and_2_out), .Q(register_12_q), .clr(in_1));
  assign controlled_buffer_19_out = not_1_out ? controlled_buffer_21_out : 10'bz;  // Controlled_Buffer controlled_buffer_23
  assign controlled_buffer_21_out = not_3_out ? register_14_q : 10'bz;  // Controlled_Buffer controlled_buffer_24
  Multiplexer #(.select(4)) multiplexer_4 (
    .in0(1'b0), .in1(1'b1), .in2(1'b0), .in3(1'b0), .in4(1'b0), .in5(1'b0), .in6(1'b0), .in7(1'b0),
    .in8(1'b0), .in9(1'b0), .in10(1'b0), .in11(1'b0), .in12(1'b0), .in13(1'b0), .in14(1'b0), .in15(1'b0),
    .out(multiplexer_4_out), .sel(bitselector_1_out));
  Register #(.width(10)) register_13 (
    .D(controlled_buffer_25_out), .en(multiplexer_21_out), .clk(and_2_out), .Q(register_13_q), .clr(in_1));
  assign controlled_buffer_25_out = not_2_out ? register_12_q : 10'bz;  // Controlled_Buffer controlled_buffer_25
  assign controlled_buffer_26_out = not_2_out ? controlled_buffer_25_out : 10'bz;  // Controlled_Buffer controlled_buffer_26
  Register #(.width(10)) register_14 (
    .D(controlled_buffer_26_out), .en(multiplexer_21_out), .clk(and_2_out), .Q(register_14_q), .clr(in_1));
  Register #(.width(10)) register_15 (
    .D(controlled_buffer_27_out), .en(multiplexer_21_out), .clk(and_2_out), .clr(in_1));  // open: Q
  assign controlled_buffer_27_out = not_2_out ? register_13_q : 10'bz;  // Controlled_Buffer controlled_buffer_27
  assign controlled_buffer_25_out = not_1_out ? controlled_buffer_26_out : 10'bz;  // Controlled_Buffer controlled_buffer_28
  assign controlled_buffer_29_out = not_2_out ? controlled_buffer_27_out : 10'bz;  // Controlled_Buffer controlled_buffer_29
  assign controlled_buffer_26_out = not_3_out ? register_16_q : 10'bz;  // Controlled_Buffer controlled_buffer_30
  Register #(.width(10)) register_16 (
    .D(controlled_buffer_29_out), .en(multiplexer_21_out), .clk(and_2_out), .Q(register_16_q), .clr(in_1));
  assign controlled_buffer_27_out = not_1_out ? controlled_buffer_29_out : 10'bz;  // Controlled_Buffer controlled_buffer_31
  Multiplexer #(.select(4)) multiplexer_5 (
    .in0(1'b0), .in1(1'b0), .in2(1'b1), .in3(1'b1), .in4(1'b1), .in5(1'b1), .in6(1'b1), .in7(1'b1),
    .in8(1'b1), .in9(1'b1), .in10(1'b0), .in11(1'b0), .in12(1'b0), .in13(1'b0), .in14(1'b1), .in15(1'b1),
    .out(multiplexer_5_out), .sel(bitselector_1_out));
  BitSelector #(.group(10), .width(16)) bitselector_2 (.in(rom_1_data), .out(bitselector_2_out), .sel(1'b0));
  Multiplexer #(.width(2)) multiplexer_6 (.in0(2'b00), .in1(2'b10), .out(multiplexer_6_out), .sel(multiplexer_22_out));
  Multiplexer #(.width(2)) multiplexer_7 (.in0(2'b00), .out(multiplexer_7_out), .sel(or_2_out));  // open: in1
  Multiplexer multiplexer_8 (.in0(1'b0), .in1(multiplexer_35_out), .out(multiplexer_8_out), .sel(multiplexer_20_out));
  Multiplexer #(.select(2), .width(10)) multiplexer_9 (
    .in0(adder_1_out), .in1(bitselector_2_out), .in2(register_2_q), .out(multiplexer_9_out), .sel(or_1_out));  // open: in3
  assign or_1_out = multiplexer_7_out | multiplexer_6_out;  // OR_Gate or_1, 2 bits wide
  or or_2 (or_2_out, multiplexer_8_out, multiplexer_19_out);
  and and_1 (and_1_out, clock_1_out, not_5_out);
  Clock clock_1 (.out(clock_1_out));
  Multiplexer #(.select(4)) multiplexer_10 (
    .in0(1'b0), .in1(1'b0), .in2(1'b0), .in3(1'b0), .in4(1'b0), .in5(1'b0), .in6(1'b0), .in7(1'b0),
    .in8(1'b1), .in9(1'b0), .in10(1'b0), .in11(1'b0), .in12(1'b0), .in13(1'b0), .in14(1'b0), .in15(1'b0),
    .out(multiplexer_10_out), .sel(bitselector_1_out));
  Register #(.width(10)) register_17 (.D(multiplexer_9_out), .en(1'b1), .clk(and_2_out), .Q(register_17_q), .clr(in_1));
  and and_2 (and_2_out, and_1_out, not_4_out);
  not not_4 (not_4_out, in_1);
  not not_5 (not_5_out, multiplexer_4_out);
  ROM #(.addrWidth(10), .dataWidth(16)) rom_1 (.addr(register_17_q), .data(rom_1_data));
  Adder #(.width(10)) adder_1 (.a(10'h1), .b(register_17_q), .out(adder_1_out));  // open: cin, cout
  Multiplexer #(.select(4)) multiplexer_11 (
    .in0(1'b0), .in1(1'b0), .in2(1'b0), .in3(1'b0), .in4(1'b0), .in5(1'b0), .in6(1'b0), .in7(1'b0),
    .in8(1'b1), .in9(1'b1), .in10(1'b0), .in11(1'b0), .in12(1'b0), .in13(1'b0), .in14(1'b0), .in15(1'b0),
    .out(multiplexer_11_out), .sel(bitselector_1_out));
  BitSelector #(.group(2), .width(1)) bitselector_3 (.in(multiplexer_23_out), .out(bitselector_3_out), .sel(1'b0));
  Multiplexer #(.select(4)) multiplexer_12 (
    .in0(1'b0), .in1(1'b0), .in2(1'b0), .in3(1'b0), .in4(1'b0), .in5(1'b0), .in6(1'b0), .in7(1'b0),
    .in8(1'b0), .in9(1'b1), .in10(1'b0), .in11(1'b0), .in12(1'b0), .in13(1'b0), .in14(1'b1), .in15(1'b1),
    .out(multiplexer_12_out), .sel(bitselector_1_out));
  BitSelector #(.group(8), .width(16)) bitselector_4 (.in(rom_1_data), .out(bitselector_4_out), .sel(1'b0));
  BitSelector #(.group(4), .width(16)) bitselector_5 (.in(rom_1_data), .out(bitselector_5_out), .sel(2'b00));
  BitSelector #(.group(8), .width(4)) bitselector_6 (.in(bitselector_5_out), .out(bitselector_6_out), .sel(1'b0));
  BitSelector #(.group(4), .width(16)) bitselector_7 (.in(rom_1_data), .out(bitselector_7_out), .sel(2'b01));
  BitSelector #(.group(4), .width(16)) bitselector_8 (.in(rom_1_data), .out(bitselector_8_out), .sel(2'b00));
  Multiplexer #(.width(4)) multiplexer_13 (
    .in0(bitselector_8_out), .in1(bitselector_9_out), .out(multiplexer_13_out), .sel(multiplexer_11_out));
  BitSelector #(.group(4), .width(16)) bitselector_9 (.in(rom_1_data), .out(bitselector_9_out), .sel(2'b10));
  Multiplexer #(.width(2)) multiplexer_14 (
    .in0(bitselector_3_out), .in1(2'b11), .out(multiplexer_14_out), .sel(multiplexer_30_out));
  Multiplexer #(.width(8)) multiplexer_15 (
    .in0(bitselector_4_out), .in1(bitselector_6_out), .out(multiplexer_15_out), .sel(multiplexer_23_out));
  Multiplexer #(.width(8)) multiplexer_16 (
    .in0(multiplexer_32_out), .in1(bitselector_4_out), .out(multiplexer_16_out), .sel(multiplexer_10_out));
  Multiplexer #(.width(8)) multiplexer_17 (
    .in0(multiplexer_16_out), .in1(ram_1_dout), .out(multiplexer_17_out), .sel(multiplexer_23_out));
  Demultiplexer #(.select(4)) demultiplexer_1 (
    .out1(demultiplexer_1_out1), .out2(demultiplexer_1_out2), .out3(demultiplexer_1_out3),
    .out4(demultiplexer_1_out4), .out5(demultiplexer_1_out5), .out6(demultiplexer_1_out6),
    .out7(demultiplexer_1_out7), .out8(demultiplexer_1_out8), .out9(demultiplexer_1_out9),
    .out10(demultiplexer_1_out10), .out11(demultiplexer_1_out11), .out12(demultiplexer_1_out12),
    .out13(demultiplexer_1_out13), .out14(demultiplexer_1_out14), .out15(demultiplexer_1_out15),
    .in(multiplexer_5_out), .sel(multiplexer_18_out));  // open: out0
  Multiplexer #(.select(2), .width(4)) multiplexer_18 (
    .in0(multiplexer_13_out), .in1(bitselector_7_out), .in2(4'b0000), .in3(4'b0000),
    .out(multiplexer_18_out), .sel(multiplexer_14_out));
  Multiplexer #(.select(4)) multiplexer_19 (
    .in0(1'b0), .in1(1'b0), .in2(1'b0), .in3(1'b0), .in4(1'b0), .in5(1'b0), .in6(1'b0), .in7(1'b0),
    .in8(1'b0), .in9(1'b0), .in10(1'b1), .in11(1'b0), .in12(1'b1), .in13(1'b0), .in14(1'b0), .in15(1'b0),
    .out(multiplexer_19_out), .sel(bitselector_1_out));
  Register register_18 (
    .D(multiplexer_17_out), .en(demultiplexer_1_out1), .clk(and_2_out), .Q(register_18_q), .clr(in_1));
  Register register_19 (
    .D(multiplexer_17_out), .en(demultiplexer_1_out2), .clk(and_2_out), .Q(register_19_q), .clr(in_1));
  Register register_20 (
    .D(multiplexer_17_out), .en(demultiplexer_1_out3), .clk(and_2_out), .Q(register_20_q), .clr(in_1));
  Multiplexer #(.select(4)) multiplexer_20 (
    .in0(1'b0), .in1(1'b0), .in2(1'b0), .in3(1'b0), .in4(1'b0), .in5(1'b0), .in6(1'b0), .in7(1'b0),
    .in8(1'b0), .in9(1'b0), .in10(1'b0), .in11(1'b1), .in12(1'b0), .in13(1'b0), .in14(1'b0), .in15(1'b0),
    .out(multiplexer_20_out), .sel(bitselector_1_out));
  Register register_21 (
    .D(multiplexer_17_out), .en(demultiplexer_1_out4), .clk(and_2_out), .Q(register_21_q), .clr(in_1));
  Register register_22 (
    .D(multiplexer_17_out), .en(demultiplexer_1_out5), .clk(and_2_out), .Q(register_22_q), .clr(in_1));
  Register register_23 (
    .D(multiplexer_17_out), .en(demultiplexer_1_out6), .clk(and_2_out), .Q(register_23_q), .clr(in_1));
  Register register_24 (
    .D(multiplexer_17_out), .en(demultiplexer_1_out7), .clk(and_2_out), .Q(register_24_q), .clr(in_1));
  Register register_25 (
    .D(multiplexer_17_out), .en(demultiplexer_1_out8), .clk(and_2_out), .Q(register_25_q), .clr(in_1));
  Register register_26 (
    .D(multiplexer_17_out), .en(demultiplexer_1_out9), .clk(and_2_out), .Q(register_26_q), .clr(in_1));
  Multiplexer #(.select(4)) multiplexer_21 (
    .in0(1'b0), .in1(1'b0), .in2(1'b0), .in3(1'b0), .in4(1'b0), .in5(1'b0), .in6(1'b0), .in7(1'b0),
    .in8(1'b0), .in9(1'b0), .in10(1'b0), .in11(1'b0), .in12(1'b1), .in13(1'b1), .in14(1'b0), .in15(1'b0),
    .out(multiplexer_21_out), .sel(bitselector_1_out));
  Register register_27 (
    .D(multiplexer_17_out), .en(demultiplexer_1_out10), .clk(and_2_out), .Q(register_27_q), .clr(in_1));
  Register register_28 (
    .D(multiplexer_17_out), .en(demultiplexer_1_out11), .clk(and_2_out), .Q(register_28_q), .clr(in_1));
  Register register_29 (
    .D(multiplexer_17_out), .en(demultiplexer_1_out12), .clk(and_2_out), .Q(register_29_q), .clr(in_1));
  Multiplexer #(.select(4)) multiplexer_22 (
    .in0(1'b0), .in1(1'b0), .in2(1'b0), .in3(1'b0), .in4(1'b0), .in5(1'b0), .in6(1'b0), .in7(1'b0),
    .in8(1'b0), .in9(1'b0), .in10(1'b0), .in11(1'b0), .in12(1'b0), .in13(1'b1), .in14(1'b0), .in15(1'b0),
    .out(multiplexer_22_out), .sel(bitselector_1_out));
  Register register_30 (
    .D(multiplexer_17_out), .en(demultiplexer_1_out13), .clk(and_2_out), .Q(register_30_q), .clr(in_1));
  Register register_31 (
    .D(multiplexer_17_out), .en(demultiplexer_1_out14), .clk(and_2_out), .Q(register_31_q), .clr(in_1));
  Register register_32 (
    .D(multiplexer_17_out), .en(demultiplexer_1_out15), .clk(and_2_out), .Q(register_32_q), .clr(in_1));
  Multiplexer #(.select(4)) multiplexer_23 (
    .in0(1'b0), .in1(1'b0), .in2(1'b0), .in3(1'b0), .in4(1'b0), .in5(1'b0), .in6(1'b0), .in7(1'b0),
    .in8(1'b0), .in9(1'b0), .in10(1'b0), .in11(1'b0), .in12(1'b0), .in13(1'b0), .in14(1'b1), .in15(1'b1),
    .out(multiplexer_23_out), .sel(bitselector_1_out));
  BitSelector #(.group(4), .width(16)) bitselector_10 (.in(rom_1_data), .out(bitselector_10_out), .sel(2'b01));
  Multiplexer #(.select(4), .width(8)) multiplexer_24 (
    .in0({8{1'b0}}), .in1(register_18_q), .in2(register_19_q), .in3(register_20_q), .in4(register_21_q),
    .in5(register_22_q), .in6(register_23_q), .in7(register_24_q), .in8(register_25_q), .in9(register_26_q),
    .in10(register_27_q), .in11(register_28_q), .in12(register_29_q), .in13(register_30_q),
    .in14(register_31_q), .in15(register_32_q), .out(multiplexer_24_out), .sel(bitselector_11_out));
  Multiplexer #(.select(4), .width(8)) multiplexer_25 (
    .in0({8{1'b0}}), .in1(register_18_q), .in2(register_19_q), .in3(register_20_q), .in4(register_21_q),
    .in5(register_22_q), .in6(register_23_q), .in7(register_24_q), .in8(register_25_q), .in9(register_26_q),
    .in10(register_27_q), .in11(register_28_q), .in12(register_29_q), .in13(register_30_q),
    .in14(register_31_q), .in15(register_32_q), .out(multiplexer_25_out), .sel(bitselector_10_out));
  BitSelector #(.group(4), .width(16)) bitselector_11 (.in(rom_1_data), .out(bitselector_11_out), .sel(2'b10));
  Multiplexer #(.select(4)) multiplexer_26 (
    .in0(1'b0), .in1(1'b0), .in2(1'b0), .in3(1'b0), .in4(1'b0), .in5(1'b0), .in6(1'b0), .in7(1'b0),
    .in8(1'b0), .in9(1'b0), .in10(1'b0), .in11(1'b0), .in12(1'b0), .in13(1'b0), .in14(1'b1), .in15(1'b0),
    .out(multiplexer_26_out), .sel(bitselector_1_out));
  Multiplexer #(.width(8)) multiplexer_27 (
    .in0({8{1'b0}}), .in1(multiplexer_24_out), .out(multiplexer_27_out), .sel(multiplexer_5_out));
  Multiplexer #(.width(8)) multiplexer_28 (
    .in0({8{1'b0}}), .in1(multiplexer_29_out), .out(multiplexer_28_out), .sel(multiplexer_5_out));
  Multiplexer #(.width(8)) multiplexer_29 (
    .in0(multiplexer_25_out), .in1(multiplexer_15_out), .out(multiplexer_29_out), .sel(multiplexer_12_out));
  BitSelector #(.group(3), .width(1)) bitselector_12 (.in(multiplexer_1_out), .out(bitselector_12_out), .sel(1'b0));
  BitSelector #(.group(3), .width(1)) bitselector_13 (.in(multiplexer_2_out), .out(bitselector_13_out), .sel(1'b0));
  BitSelector #(.group(3), .width(1)) bitselector_14 (.in(multiplexer_3_out), .out(bitselector_14_out), .sel(1'b0));
  Adder adder_2 (.a(multiplexer_27_out), .b(multiplexer_28_out), .out(adder_2_out), .cout(adder_2_cout));  // open: cin
  Subtractor subtractor_1 (
    .a(multiplexer_27_out), .b(multiplexer_28_out), .out(subtractor_1_out), .bout(subtractor_1_bout));  // open: bin
  assign and_3_out = multiplexer_27_out & multiplexer_28_out;  // AND_Gate and_3, 8 bits wide
  Shifter #(.shift("lr")) shifter_1 (.in(multiplexer_27_out), .\dist (3'b001), .out(shifter_1_out));
  Shifter #(.width(3)) shifter_2 (.in(bitselector_13_out), .\dist (2'b01), .out(shifter_2_out));
  Shifter #(.width(3)) shifter_3 (.in(bitselector_14_out), .\dist (2'b10), .out(shifter_3_out));
  assign nor_1_out = ~(multiplexer_27_out | multiplexer_28_out);  // NOR_Gate nor_1, 8 bits wide
  assign xor_1_out = multiplexer_27_out ^ multiplexer_28_out;  // XOR_Gate xor_1, 8 bits wide
  assign or_3_out = shifter_2_out | shifter_3_out;  // OR_Gate or_3, 3 bits wide
  Multiplexer #(.select(4)) multiplexer_30 (
    .in0(1'b0), .in1(1'b0), .in2(1'b0), .in3(1'b0), .in4(1'b0), .in5(1'b0), .in6(1'b0), .in7(1'b0),
    .in8(1'b0), .in9(1'b0), .in10(1'b0), .in11(1'b0), .in12(1'b0), .in13(1'b0), .in14(1'b0), .in15(1'b1),
    .out(multiplexer_30_out), .sel(bitselector_1_out));
  Multiplexer #(.select(2)) multiplexer_31 (
    .in0(1'b0), .in1(adder_2_cout), .in2(1'b0), .in3(subtractor_1_bout), .out(multiplexer_31_out),
    .sel(multiplexer_33_out));
  Multiplexer #(.select(3), .width(8)) multiplexer_32 (
    .in0(adder_2_out), .in1(subtractor_1_out), .in2(nor_1_out), .in3(and_3_out), .in4(xor_1_out),
    .in5(shifter_1_out), .out(multiplexer_32_out), .sel(or_4_out));  // open: in6, in7
  Multiplexer #(.select(3), .width(2)) multiplexer_33 (
    .in0(2'b01), .in1(2'b11), .in2(2'b00), .in3(2'b00), .in4(2'b00), .in5(2'b00), .in6(2'b00), .in7(2'b00),
    .out(multiplexer_33_out), .sel(or_4_out));
  assign or_4_out = bitselector_12_out | or_3_out;  // OR_Gate or_4, 3 bits wide
  D_Flip_Flop d_ff_1 (
    .D(multiplexer_31_out), .clk(and_2_out), .Q(d_ff_1_q), .Qn(d_ff_1_qn), .reset(in_1));  // open: preset
  D_Flip_Flop d_ff_2 (.D(or_5_out), .clk(and_2_out), .Q(d_ff_2_q), .Qn(d_ff_2_qn), .reset(in_1));  // open: preset
  Multiplexer #(.select(4)) multiplexer_34 (
    .in0(1'b0), .in1(1'b0), .in2(1'b0), .in3(1'b0), .in4(1'b0), .in5(1'b0), .in6(1'b0), .in7(1'b0),
    .in8(1'b0), .in9(1'b0), .in10(1'b0), .in11(1'b0), .in12(1'b0), .in13(1'b0), .in14(1'b0), .in15(1'b0),
    .out(multiplexer_34_out), .sel(bitselector_1_out));
  BitSelector bitselector_15 (.in(multiplexer_32_out), .out(bitselector_15_out), .sel(3'b110));
  BitSelector bitselector_16 (.in(multiplexer_32_out), .out(bitselector_16_out), .sel(3'b100));
  BitSelector bitselector_17 (.in(multiplexer_32_out), .out(bitselector_17_out), .sel(3'b010));
  BitSelector bitselector_18 (.in(multiplexer_32_out), .out(bitselector_18_out), .sel(3'b000));
  BitSelector #(.group(2), .width(16)) bitselector_19 (.in(rom_1_data), .out(bitselector_19_out), .sel(3'b101));
  Multiplexer #(.select(2)) multiplexer_35 (
    .in0(d_ff_2_qn), .in1(d_ff_2_q), .in2(d_ff_1_qn), .in3(d_ff_1_q), .out(multiplexer_35_out),
    .sel(bitselector_19_out));
  BitSelector bitselector_20 (.in(multiplexer_32_out), .out(bitselector_20_out), .sel(3'b111));
  BitSelector bitselector_21 (.in(multiplexer_32_out), .out(bitselector_21_out), .sel(3'b101));
  BitSelector bitselector_22 (.in(multiplexer_32_out), .out(bitselector_22_out), .sel(3'b011));
  BitSelector bitselector_23 (.in(multiplexer_32_out), .out(bitselector_23_out), .sel(3'b001));
  or or_5 (or_5_out, bitselector_18_out, bitselector_17_out, bitselector_16_out, bitselector_15_out, bitselector_23_out, bitselector_22_out, bitselector_21_out, bitselector_20_out);
  Multiplexer multiplexer_36 (.in0(multiplexer_26_out), .in1(in_1), .out(multiplexer_36_out), .sel(in_1));
  Multiplexer multiplexer_37 (.in0(and_2_out), .in1(in_1), .out(multiplexer_37_out), .sel(in_1));
  RAM ram_1 (
    .addr(multiplexer_32_out), .we(multiplexer_30_out), .oe(multiplexer_36_out), .clk(multiplexer_37_out),
    .din(multiplexer_25_out), .dout(ram_1_dout));
  // also tied to GND on the sheet: {controlled_buffer_29_out[0], controlled_buffer_29_out[1], controlled_buffer_29_out[2], controlled_buffer_29_out[3], controlled_buffer_29_out[4], controlled_buffer_29_out[5], controlled_buffer_29_out[6], controlled_buffer_29_out[7], controlled_buffer_29_out[8], controlled_buffer_29_out[9]}

  // Notes on the sheet:
  //   contents of rom_1 (hex, n*v repeats v):
  //   8105 8209 2123 ff30 ef40 2f40
endmodule
