// Logisim project l_8_bit_computer.circ as structural Verilog: 6 circuits, main circuit main
module main (
  input  in_1
);

  wire alu_1_alufo, clock_1_out, com_1_com0, com_1_com1, com_1_com2, com_1_com3, com_1_com4, com_1_com5,
       com_1_com6, com_1_com7, com_1_com8, com_1_com9, com_1_coma, com_1_comb, com_1_comc, com_1_comd,
       com_1_come, pc_1_pct;
  wire [1:0] bitselector_3_out, bitselector_12_out, multiplexer_6_out;
  wire [3:0] bitselector_1_out, bitselector_5_out, bitselector_7_out, bitselector_8_out, bitselector_9_out,
       bitselector_10_out, bitselector_11_out, multiplexer_4_out, multiplexer_5_out;
  wire [7:0] alu_1_alur, bitselector_4_out, bitselector_6_out, multiplexer_1_out, multiplexer_2_out,
       multiplexer_3_out, multiplexer_7_out, r_1_rrd0, r_1_rrd1, ram_1_dout;
  wire [9:0] bitselector_2_out, cs_1_csdo, pc_1_pcc0;
  wire [15:0] rom_1_data;

  BitSelector #(.group(4), .width(16)) bitselector_1 (.in(rom_1_data), .out(bitselector_1_out), .sel(2'b11));
  COM com_1 (
    .in_1(bitselector_1_out), .COM4(com_1_com4), .COM5(com_1_com5), .COM6(com_1_com6), .COM7(com_1_com7),
    .COM8(com_1_com8), .COM9(com_1_com9), .COMa(com_1_coma), .COMb(com_1_comb), .COM0(com_1_com0),
    .COMc(com_1_comc), .COMd(com_1_comd), .COMe(com_1_come), .COM1(com_1_com1), .COM2(com_1_com2),
    .COM3(com_1_com3));  // open: COMf
  Clock clock_1 (.out(clock_1_out));
  BitSelector #(.group(10), .width(16)) bitselector_2 (.in(rom_1_data), .out(bitselector_2_out), .sel(1'b0));
  ROM #(.addrWidth(10), .dataWidth(16)) rom_1 (.addr(pc_1_pcc0), .data(rom_1_data));
  CS cs_1 (.CSwr(com_1_comb), .CSdi(pc_1_pcc0), .CSe(com_1_coma), .CSc(pc_1_pct), .CSr(in_1), .CSdo(cs_1_csdo));
  PC pc_1 (
    .PCd0(bitselector_2_out), .PCd1(cs_1_csdo), .PCd2(alu_1_alufo), .PCa0(com_1_com9), .PCa1(com_1_com8),
    .PCa2(com_1_comb), .PCh(com_1_com3), .PCc(clock_1_out), .PCr(in_1), .PCt(pc_1_pct), .PCc0(pc_1_pcc0));
  BitSelector #(.group(2), .width(16)) bitselector_3 (.in(rom_1_data), .out(bitselector_3_out), .sel(3'b101));
  Multiplexer #(.width(8)) multiplexer_1 (
    .in0(bitselector_4_out), .in1(bitselector_6_out), .out(multiplexer_1_out), .sel(com_1_comc));
  BitSelector #(.group(8), .width(16)) bitselector_4 (.in(rom_1_data), .out(bitselector_4_out), .sel(1'b0));
  BitSelector #(.group(4), .width(16)) bitselector_5 (.in(rom_1_data), .out(bitselector_5_out), .sel(2'b00));
  BitSelector #(.group(8), .width(4)) bitselector_6 (.in(bitselector_5_out), .out(bitselector_6_out), .sel(1'b0));
  BitSelector #(.group(4), .width(16)) bitselector_7 (.in(rom_1_data), .out(bitselector_7_out), .sel(2'b00));
  BitSelector #(.group(4), .width(16)) bitselector_8 (.in(rom_1_data), .out(bitselector_8_out), .sel(2'b10));
  BitSelector #(.group(4), .width(16)) bitselector_9 (.in(rom_1_data), .out(bitselector_9_out), .sel(2'b01));
  BitSelector #(.group(4), .width(16)) bitselector_10 (.in(rom_1_data), .out(bitselector_10_out), .sel(2'b10));
  BitSelector #(.group(4), .width(16)) bitselector_11 (.in(rom_1_data), .out(bitselector_11_out), .sel(2'b01));
  Multiplexer #(.width(8)) multiplexer_2 (
    .in0(alu_1_alur), .in1(bitselector_4_out), .out(multiplexer_2_out), .sel(com_1_com5));
  Multiplexer #(.width(8)) multiplexer_3 (
    .in0(multiplexer_2_out), .in1(ram_1_dout), .out(multiplexer_3_out), .sel(com_1_comc));
  Multiplexer #(.width(4)) multiplexer_4 (
    .in0(bitselector_7_out), .in1(bitselector_8_out), .out(multiplexer_4_out), .sel(com_1_com6));
  Multiplexer #(.select(2), .width(4)) multiplexer_5 (
    .in0(multiplexer_4_out), .in1(bitselector_9_out), .in2(4'b0000), .in3(4'b0000), .out(multiplexer_5_out),
    .sel(multiplexer_6_out));
  BitSelector #(.group(2), .width(1)) bitselector_12 (.in(com_1_comc), .out(bitselector_12_out), .sel(1'b0));
  Multiplexer #(.width(2)) multiplexer_6 (
    .in0(bitselector_12_out), .in1(2'b11), .out(multiplexer_6_out), .sel(com_1_come));
  R r_1 (
    .Rwd(multiplexer_3_out), .Rwa(multiplexer_5_out), .Re(com_1_com4), .Rra0(bitselector_10_out),
    .Rra1(bitselector_11_out), .Rc(pc_1_pct), .Rr(in_1), .Rrd0(r_1_rrd0), .Rrd1(r_1_rrd1));
  Multiplexer #(.width(8)) multiplexer_7 (
    .in0(r_1_rrd1), .in1(multiplexer_1_out), .out(multiplexer_7_out), .sel(com_1_com7));
  RAM ram_1 (.addr(alu_1_alur), .we(com_1_come), .oe(com_1_comd), .clk(pc_1_pct), .din(r_1_rrd1), .dout(ram_1_dout));
  ALU alu_1 (
    .ALUw0(r_1_rrd0), .ALUw1(multiplexer_7_out), .ALUd0(com_1_com0), .ALUd1(com_1_com1), .ALUd2(com_1_com2),
    .ALUfi(bitselector_3_out), .ALUc(pc_1_pct), .ALUr(alu_1_alur), .ALUfo(alu_1_alufo));

  // Notes on the sheet:
  //   contents of rom_1 (hex, n*v repeats v):
  //   8101 8201 2121 2122 a002
endmodule

module COM (
  input  [3:0] in_1,
  output COM0,
  output COM1,
  output COM2,
  output COM3,
  output COM4,
  output COM5,
  output COM6,
  output COM7,
  output COM8,
  output COM9,
  output COMa,
  output COMb,
  output COMc,
  output COMd,
  output COMe,
  output COMf
);

  Multiplexer #(.select(4)) multiplexer_1 (
    .in0(1'b0), .in1(1'b0), .in2(1'b0), .in3(1'b1), .in4(1'b0), .in5(1'b1), .in6(1'b0), .in7(1'b1),
    .in8(1'b0), .in9(1'b0), .in10(1'b0), .in11(1'b0), .in12(1'b0), .in13(1'b0), .in14(1'b0), .in15(1'b0),
    .out(COM0), .sel(in_1));
  Multiplexer #(.select(4)) multiplexer_2 (
    .in0(1'b0), .in1(1'b0), .in2(1'b0), .in3(1'b0), .in4(1'b1), .in5(1'b1), .in6(1'b0), .in7(1'b0),
    .in8(1'b0), .in9(1'b0), .in10(1'b0), .in11(1'b0), .in12(1'b0), .in13(1'b0), .in14(1'b0), .in15(1'b0),
    .out(COM1), .sel(in_1));
  Multiplexer #(.select(4)) multiplexer_3 (
    .in0(1'b0), .in1(1'b0), .in2(1'b0), .in3(1'b0), .in4(1'b0), .in5(1'b0), .in6(1'b1), .in7(1'b1),
    .in8(1'b0), .in9(1'b0), .in10(1'b0), .in11(1'b0), .in12(1'b0), .in13(1'b0), .in14(1'b0), .in15(1'b0),
    .out(COM2), .sel(in_1));
  Multiplexer #(.select(4)) multiplexer_4 (
    .in0(1'b0), .in1(1'b1), .in2(1'b0), .in3(1'b0), .in4(1'b0), .in5(1'b0), .in6(1'b0), .in7(1'b0),
    .in8(1'b0), .in9(1'b0), .in10(1'b0), .in11(1'b0), .in12(1'b0), .in13(1'b0), .in14(1'b0), .in15(1'b0),
    .out(COM3), .sel(in_1));
  Multiplexer #(.select(4)) multiplexer_5 (
    .in0(1'b0), .in1(1'b0), .in2(1'b1), .in3(1'b1), .in4(1'b1), .in5(1'b1), .in6(1'b1), .in7(1'b1),
    .in8(1'b1), .in9(1'b1), .in10(1'b0), .in11(1'b0), .in12(1'b0), .in13(1'b0), .in14(1'b1), .in15(1'b1),
    .out(COM4), .sel(in_1));
  Multiplexer #(.select(4)) multiplexer_6 (
    .in0(1'b0), .in1(1'b0), .in2(1'b0), .in3(1'b0), .in4(1'b0), .in5(1'b0), .in6(1'b0), .in7(1'b0),
    .in8(1'b1), .in9(1'b0), .in10(1'b0), .in11(1'b0), .in12(1'b0), .in13(1'b0), .in14(1'b0), .in15(1'b0),
    .out(COM5), .sel(in_1));
  Multiplexer #(.select(4)) multiplexer_7 (
    .in0(1'b0), .in1(1'b0), .in2(1'b0), .in3(1'b0), .in4(1'b0), .in5(1'b0), .in6(1'b0), .in7(1'b0),
    .in8(1'b1), .in9(1'b1), .in10(1'b0), .in11(1'b0), .in12(1'b0), .in13(1'b0), .in14(1'b0), .in15(1'b0),
    .out(COM6), .sel(in_1));
  Multiplexer #(.select(4)) multiplexer_8 (
    .in0(1'b0), .in1(1'b0), .in2(1'b0), .in3(1'b0), .in4(1'b0), .in5(1'b0), .in6(1'b0), .in7(1'b0),
    .in8(1'b0), .in9(1'b1), .in10(1'b0), .in11(1'b0), .in12(1'b0), .in13(1'b0), .in14(1'b1), .in15(1'b1),
    .out(COM7), .sel(in_1));
  Multiplexer #(.select(4)) multiplexer_9 (
    .in0(1'b0), .in1(1'b0), .in2(1'b0), .in3(1'b0), .in4(1'b0), .in5(1'b0), .in6(1'b0), .in7(1'b0),
    .in8(1'b0), .in9(1'b0), .in10(1'b1), .in11(1'b0), .in12(1'b1), .in13(1'b0), .in14(1'b0), .in15(1'b0),
    .out(COM8), .sel(in_1));
  Multiplexer #(.select(4)) multiplexer_10 (
    .in0(1'b0), .in1(1'b0), .in2(1'b0), .in3(1'b0), .in4(1'b0), .in5(1'b0), .in6(1'b0), .in7(1'b0),
    .in8(1'b0), .in9(1'b0), .in10(1'b0), .in11(1'b1), .in12(1'b0), .in13(1'b0), .in14(1'b0), .in15(1'b0),
    .out(COM9), .sel(in_1));
  Multiplexer #(.select(4)) multiplexer_11 (
    .in0(1'b0), .in1(1'b0), .in2(1'b0), .in3(1'b0), .in4(1'b0), .in5(1'b0), .in6(1'b0), .in7(1'b0),
    .in8(1'b0), .in9(1'b0), .in10(1'b0), .in11(1'b0), .in12(1'b1), .in13(1'b1), .in14(1'b0), .in15(1'b0),
    .out(COMa), .sel(in_1));
  Multiplexer #(.select(4)) multiplexer_12 (
    .in0(1'b0), .in1(1'b0), .in2(1'b0), .in3(1'b0), .in4(1'b0), .in5(1'b0), .in6(1'b0), .in7(1'b0),
    .in8(1'b0), .in9(1'b0), .in10(1'b0), .in11(1'b0), .in12(1'b0), .in13(1'b1), .in14(1'b0), .in15(1'b0),
    .out(COMb), .sel(in_1));
  Multiplexer #(.select(4)) multiplexer_13 (
    .in0(1'b0), .in1(1'b0), .in2(1'b0), .in3(1'b0), .in4(1'b0), .in5(1'b0), .in6(1'b0), .in7(1'b0),
    .in8(1'b0), .in9(1'b0), .in10(1'b0), .in11(1'b0), .in12(1'b0), .in13(1'b0), .in14(1'b1), .in15(1'b1),
    .out(COMc), .sel(in_1));
  Multiplexer #(.select(4)) multiplexer_14 (
    .in0(1'b0), .in1(1'b0), .in2(1'b0), .in3(1'b0), .in4(1'b0), .in5(1'b0), .in6(1'b0), .in7(1'b0),
    .in8(1'b0), .in9(1'b0), .in10(1'b0), .in11(1'b0), .in12(1'b0), .in13(1'b0), .in14(1'b1), .in15(1'b0),
    .out(COMd), .sel(in_1));
  Multiplexer #(.select(4)) multiplexer_15 (
    .in0(1'b0), .in1(1'b0), .in2(1'b0), .in3(1'b0), .in4(1'b0), .in5(1'b0), .in6(1'b0), .in7(1'b0),
    .in8(1'b0), .in9(1'b0), .in10(1'b0), .in11(1'b0), .in12(1'b0), .in13(1'b0), .in14(1'b0), .in15(1'b1),
    .out(COMe), .sel(in_1));
  Multiplexer #(.select(4)) multiplexer_16 (
    .in0(1'b0), .in1(1'b0), .in2(1'b0), .in3(1'b0), .in4(1'b0), .in5(1'b0), .in6(1'b0), .in7(1'b0),
    .in8(1'b0), .in9(1'b0), .in10(1'b0), .in11(1'b0), .in12(1'b0), .in13(1'b0), .in14(1'b0), .in15(1'b0),
    .out(COMf), .sel(in_1));
endmodule

module CS (
  input  CSwr,
  input  [9:0] CSdi,
  input  CSe,
  input  CSc,
  input  CSr,
  output [9:0] CSdo
);

  wire not_1_out, not_2_out, not_3_out;
  wire [9:0] controlled_buffer_1_out, controlled_buffer_2_out, controlled_buffer_5_out,
       controlled_buffer_6_out, controlled_buffer_7_out, controlled_buffer_9_out, controlled_buffer_11_out,
       controlled_buffer_13_out, controlled_buffer_15_out, controlled_buffer_17_out,
       controlled_buffer_21_out, controlled_buffer_22_out, controlled_buffer_23_out,
       controlled_buffer_25_out, controlled_buffer_27_out, controlled_buffer_29_out,
       controlled_buffer_31_out, controlled_buffer_33_out, controlled_buffer_36_out,
       controlled_buffer_37_out, controlled_buffer_38_out, controlled_buffer_40_out,
       controlled_buffer_42_out, controlled_buffer_44_out, controlled_buffer_46_out,
       controlled_buffer_48_out, controlled_buffer_52_out, controlled_buffer_53_out,
       controlled_buffer_54_out, controlled_buffer_56_out, controlled_buffer_58_out,
       controlled_buffer_60_out, register_2_q, register_3_q, register_4_q, register_5_q, register_6_q,
       register_7_q, register_8_q, register_9_q, register_10_q, register_11_q, register_12_q, register_13_q,
       register_14_q, register_15_q, register_16_q, register_17_q, register_18_q, register_19_q,
       register_20_q, register_21_q, register_22_q, register_23_q, register_24_q, register_25_q,
       register_26_q, register_27_q, register_28_q, register_29_q, register_30_q, register_32_q;

  not not_1 (not_1_out, not_2_out);
  not not_2 (not_2_out, CSwr);
  not not_3 (not_3_out, not_2_out);
  assign controlled_buffer_1_out = not_2_out ? CSdi : 10'bz;  // Controlled_Buffer controlled_buffer_1
  assign controlled_buffer_2_out = not_2_out ? controlled_buffer_1_out : 10'bz;  // Controlled_Buffer controlled_buffer_2
  Register #(.width(10)) register_1 (.D(controlled_buffer_2_out), .en(CSe), .clk(CSc), .Q(CSdo), .clr(CSr));
  Register #(.width(10)) register_2 (.D(controlled_buffer_1_out), .en(CSe), .clk(CSc), .Q(register_2_q), .clr(CSr));
  assign controlled_buffer_1_out = not_1_out ? controlled_buffer_2_out : 10'bz;  // Controlled_Buffer controlled_buffer_3
  assign controlled_buffer_2_out = not_3_out ? register_4_q : 10'bz;  // Controlled_Buffer controlled_buffer_4
  Register #(.width(10)) register_3 (.D(controlled_buffer_5_out), .en(CSe), .clk(CSc), .Q(register_3_q), .clr(CSr));
  assign controlled_buffer_5_out = not_2_out ? register_2_q : 10'bz;  // Controlled_Buffer controlled_buffer_5
  assign controlled_buffer_6_out = not_2_out ? controlled_buffer_5_out : 10'bz;  // Controlled_Buffer controlled_buffer_6
  Register #(.width(10)) register_4 (.D(controlled_buffer_6_out), .en(CSe), .clk(CSc), .Q(register_4_q), .clr(CSr));
  Register #(.width(10)) register_5 (.D(controlled_buffer_7_out), .en(CSe), .clk(CSc), .Q(register_5_q), .clr(CSr));
  assign controlled_buffer_7_out = not_2_out ? register_3_q : 10'bz;  // Controlled_Buffer controlled_buffer_7
  assign controlled_buffer_5_out = not_1_out ? controlled_buffer_6_out : 10'bz;  // Controlled_Buffer controlled_buffer_8
  assign controlled_buffer_9_out = not_2_out ? controlled_buffer_7_out : 10'bz;  // Controlled_Buffer controlled_buffer_9
  assign controlled_buffer_6_out = not_3_out ? register_6_q : 10'bz;  // Controlled_Buffer controlled_buffer_10
  Register #(.width(10)) register_6 (.D(controlled_buffer_9_out), .en(CSe), .clk(CSc), .Q(register_6_q), .clr(CSr));
  Register #(.width(10)) register_7 (.D(controlled_buffer_11_out), .en(CSe), .clk(CSc), .Q(register_7_q), .clr(CSr));
  assign controlled_buffer_11_out = not_2_out ? register_5_q : 10'bz;  // Controlled_Buffer controlled_buffer_11
  assign controlled_buffer_7_out = not_1_out ? controlled_buffer_9_out : 10'bz;  // Controlled_Buffer controlled_buffer_12
  assign controlled_buffer_13_out = not_2_out ? controlled_buffer_11_out : 10'bz;  // Controlled_Buffer controlled_buffer_13
  assign controlled_buffer_9_out = not_3_out ? register_8_q : 10'bz;  // Controlled_Buffer controlled_buffer_14
  Register #(.width(10)) register_8 (.D(controlled_buffer_13_out), .en(CSe), .clk(CSc), .Q(register_8_q), .clr(CSr));
  assign controlled_buffer_15_out = not_2_out ? register_7_q : 10'bz;  // Controlled_Buffer controlled_buffer_15
  assign controlled_buffer_11_out = not_1_out ? controlled_buffer_13_out : 10'bz;  // Controlled_Buffer controlled_buffer_16
  assign controlled_buffer_17_out = not_2_out ? controlled_buffer_15_out : 10'bz;  // Controlled_Buffer controlled_buffer_17
  assign controlled_buffer_13_out = not_3_out ? register_9_q : 10'bz;  // Controlled_Buffer controlled_buffer_18
  Register #(.width(10)) register_9 (.D(controlled_buffer_17_out), .en(CSe), .clk(CSc), .Q(register_9_q), .clr(CSr));
  Register #(.width(10)) register_10 (.D(controlled_buffer_15_out), .en(CSe), .clk(CSc), .Q(register_10_q), .clr(CSr));
  assign controlled_buffer_15_out = not_1_out ? controlled_buffer_17_out : 10'bz;  // Controlled_Buffer controlled_buffer_19
  assign controlled_buffer_17_out = not_3_out ? register_12_q : 10'bz;  // Controlled_Buffer controlled_buffer_20
  Register #(.width(10)) register_11 (.D(controlled_buffer_21_out), .en(CSe), .clk(CSc), .Q(register_11_q), .clr(CSr));
  assign controlled_buffer_21_out = not_2_out ? register_10_q : 10'bz;  // Controlled_Buffer controlled_buffer_21
  assign controlled_buffer_22_out = not_2_out ? controlled_buffer_21_out : 10'bz;  // Controlled_Buffer controlled_buffer_22
  Register #(.width(10)) register_12 (.D(controlled_buffer_22_out), .en(CSe), .clk(CSc), .Q(register_12_q), .clr(CSr));
  Register #(.width(10)) register_13 (.D(controlled_buffer_23_out), .en(CSe), .clk(CSc), .Q(register_13_q), .clr(CSr));
  assign controlled_buffer_23_out = not_2_out ? register_11_q : 10'bz;  // Controlled_Buffer controlled_buffer_23
  assign controlled_buffer_21_out = not_1_out ? controlled_buffer_22_out : 10'bz;  // Controlled_Buffer controlled_buffer_24
  assign controlled_buffer_25_out = not_2_out ? controlled_buffer_23_out : 10'bz;  // Controlled_Buffer controlled_buffer_25
  assign controlled_buffer_22_out = not_3_out ? register_14_q : 10'bz;  // Controlled_Buffer controlled_buffer_26
  Register #(.width(10)) register_14 (.D(controlled_buffer_25_out), .en(CSe), .clk(CSc), .Q(register_14_q), .clr(CSr));
  Register #(.width(10)) register_15 (.D(controlled_buffer_27_out), .en(CSe), .clk(CSc), .Q(register_15_q), .clr(CSr));
  assign controlled_buffer_27_out = not_2_out ? register_13_q : 10'bz;  // Controlled_Buffer controlled_buffer_27
  assign controlled_buffer_23_out = not_1_out ? controlled_buffer_25_out : 10'bz;  // Controlled_Buffer controlled_buffer_28
  assign controlled_buffer_29_out = not_2_out ? controlled_buffer_27_out : 10'bz;  // Controlled_Buffer controlled_buffer_29
  assign controlled_buffer_25_out = not_3_out ? register_16_q : 10'bz;  // Controlled_Buffer controlled_buffer_30
  Register #(.width(10)) register_16 (.D(controlled_buffer_29_out), .en(CSe), .clk(CSc), .Q(register_16_q), .clr(CSr));
  assign controlled_buffer_31_out = not_2_out ? register_15_q : 10'bz;  // Controlled_Buffer controlled_buffer_31
  assign controlled_buffer_27_out = not_1_out ? controlled_buffer_29_out : 10'bz;  // Controlled_Buffer controlled_buffer_32
  assign controlled_buffer_33_out = not_2_out ? controlled_buffer_31_out : 10'bz;  // Controlled_Buffer controlled_buffer_33
  Register #(.width(10)) register_17 (.D(controlled_buffer_33_out), .en(CSe), .clk(CSc), .Q(register_17_q), .clr(CSr));
  Register #(.width(10)) register_18 (.D(controlled_buffer_31_out), .en(CSe), .clk(CSc), .Q(register_18_q), .clr(CSr));
  assign controlled_buffer_31_out = not_1_out ? controlled_buffer_33_out : 10'bz;  // Controlled_Buffer controlled_buffer_34
  assign controlled_buffer_33_out = not_3_out ? register_20_q : 10'bz;  // Controlled_Buffer controlled_buffer_35
  Register #(.width(10)) register_19 (.D(controlled_buffer_36_out), .en(CSe), .clk(CSc), .Q(register_19_q), .clr(CSr));
  assign controlled_buffer_36_out = not_2_out ? register_18_q : 10'bz;  // Controlled_Buffer controlled_buffer_36
  assign controlled_buffer_37_out = not_2_out ? controlled_buffer_36_out : 10'bz;  // Controlled_Buffer controlled_buffer_37
  Register #(.width(10)) register_20 (.D(controlled_buffer_37_out), .en(CSe), .clk(CSc), .Q(register_20_q), .clr(CSr));
  Register #(.width(10)) register_21 (.D(controlled_buffer_38_out), .en(CSe), .clk(CSc), .Q(register_21_q), .clr(CSr));
  assign controlled_buffer_38_out = not_2_out ? register_19_q : 10'bz;  // Controlled_Buffer controlled_buffer_38
  assign controlled_buffer_36_out = not_1_out ? controlled_buffer_37_out : 10'bz;  // Controlled_Buffer controlled_buffer_39
  assign controlled_buffer_40_out = not_2_out ? controlled_buffer_38_out : 10'bz;  // Controlled_Buffer controlled_buffer_40
  assign controlled_buffer_37_out = not_3_out ? register_22_q : 10'bz;  // Controlled_Buffer controlled_buffer_41
  Register #(.width(10)) register_22 (.D(controlled_buffer_40_out), .en(CSe), .clk(CSc), .Q(register_22_q), .clr(CSr));
  Register #(.width(10)) register_23 (.D(controlled_buffer_42_out), .en(CSe), .clk(CSc), .Q(register_23_q), .clr(CSr));
  assign controlled_buffer_42_out = not_2_out ? register_21_q : 10'bz;  // Controlled_Buffer controlled_buffer_42
  assign controlled_buffer_38_out = not_1_out ? controlled_buffer_40_out : 10'bz;  // Controlled_Buffer controlled_buffer_43
  assign controlled_buffer_44_out = not_2_out ? controlled_buffer_42_out : 10'bz;  // Controlled_Buffer controlled_buffer_44
  assign controlled_buffer_40_out = not_3_out ? register_24_q : 10'bz;  // Controlled_Buffer controlled_buffer_45
  Register #(.width(10)) register_24 (.D(controlled_buffer_44_out), .en(CSe), .clk(CSc), .Q(register_24_q), .clr(CSr));
  assign controlled_buffer_46_out = not_2_out ? register_23_q : 10'bz;  // Controlled_Buffer controlled_buffer_46
  assign controlled_buffer_42_out = not_1_out ? controlled_buffer_44_out : 10'bz;  // Controlled_Buffer controlled_buffer_47
  assign controlled_buffer_48_out = not_2_out ? controlled_buffer_46_out : 10'bz;  // Controlled_Buffer controlled_buffer_48
  assign controlled_buffer_44_out = not_3_out ? register_25_q : 10'bz;  // Controlled_Buffer controlled_buffer_49
  Register #(.width(10)) register_25 (.D(controlled_buffer_48_out), .en(CSe), .clk(CSc), .Q(register_25_q), .clr(CSr));
  Register #(.width(10)) register_26 (.D(controlled_buffer_46_out), .en(CSe), .clk(CSc), .Q(register_26_q), .clr(CSr));
  assign controlled_buffer_46_out = not_1_out ? controlled_buffer_48_out : 10'bz;  // Controlled_Buffer controlled_buffer_50
  assign controlled_buffer_48_out = not_3_out ? register_28_q : 10'bz;  // Controlled_Buffer controlled_buffer_51
  Register #(.width(10)) register_27 (.D(controlled_buffer_52_out), .en(CSe), .clk(CSc), .Q(register_27_q), .clr(CSr));
  assign controlled_buffer_52_out = not_2_out ? register_26_q : 10'bz;  // Controlled_Buffer controlled_buffer_52
  assign controlled_buffer_53_out = not_2_out ? controlled_buffer_52_out : 10'bz;  // Controlled_Buffer controlled_buffer_53
  Register #(.width(10)) register_28 (.D(controlled_buffer_53_out), .en(CSe), .clk(CSc), .Q(register_28_q), .clr(CSr));
  Register #(.width(10)) register_29 (.D(controlled_buffer_54_out), .en(CSe), .clk(CSc), .Q(register_29_q), .clr(CSr));
  assign controlled_buffer_54_out = not_2_out ? register_27_q : 10'bz;  // Controlled_Buffer controlled_buffer_54
  assign controlled_buffer_52_out = not_1_out ? controlled_buffer_53_out : 10'bz;  // Controlled_Buffer controlled_buffer_55
  assign controlled_buffer_56_out = not_2_out ? controlled_buffer_54_out : 10'bz;  // Controlled_Buffer controlled_buffer_56
  assign controlled_buffer_53_out = not_3_out ? register_30_q : 10'bz;  // Controlled_Buffer controlled_buffer_57
  Register #(.width(10)) register_30 (.D(controlled_buffer_56_out), .en(CSe), .clk(CSc), .Q(register_30_q), .clr(CSr));
  Register #(.width(10)) register_31 (.D(controlled_buffer_58_out), .en(CSe), .clk(CSc), .clr(CSr));  // open: Q
  assign controlled_buffer_58_out = not_2_out ? register_29_q : 10'bz;  // Controlled_Buffer controlled_buffer_58
  assign controlled_buffer_54_out = not_1_out ? controlled_buffer_56_out : 10'bz;  // Controlled_Buffer controlled_buffer_59
  assign controlled_buffer_60_out = not_2_out ? controlled_buffer_58_out : 10'bz;  // Controlled_Buffer controlled_buffer_60
  assign controlled_buffer_56_out = not_3_out ? register_32_q : 10'bz;  // Controlled_Buffer controlled_buffer_61
  Register #(.width(10)) register_32 (.D(controlled_buffer_60_out), .en(CSe), .clk(CSc), .Q(register_32_q), .clr(CSr));
  assign controlled_buffer_58_out = not_1_out ? controlled_buffer_60_out : 10'bz;  // Controlled_Buffer controlled_buffer_62
  // also tied to GND on the sheet: {controlled_buffer_60_out[0], controlled_buffer_60_out[1], controlled_buffer_60_out[2], controlled_buffer_60_out[3], controlled_buffer_60_out[4], controlled_buffer_60_out[5], controlled_buffer_60_out[6], controlled_buffer_60_out[7], controlled_buffer_60_out[8], controlled_buffer_60_out[9]}
endmodule

module R (
  input  [7:0] Rwd,
  input  [3:0] Rwa,
  input  Re,
  input  [3:0] Rra0,
  input  [3:0] Rra1,
  input  Rc,
  input  Rr,
  output [7:0] Rrd0,
  output [7:0] Rrd1
);

  wire demultiplexer_1_out1, demultiplexer_1_out2, demultiplexer_1_out3, demultiplexer_1_out4,
       demultiplexer_1_out5, demultiplexer_1_out6, demultiplexer_1_out7, demultiplexer_1_out8,
       demultiplexer_1_out9, demultiplexer_1_out10, demultiplexer_1_out11, demultiplexer_1_out12,
       demultiplexer_1_out13, demultiplexer_1_out14, demultiplexer_1_out15;
  wire [7:0] multiplexer_1_out, multiplexer_2_out, register_1_q, register_2_q, register_3_q, register_4_q,
       register_5_q, register_6_q, register_7_q, register_8_q, register_9_q, register_10_q, register_11_q,
       register_12_q, register_13_q, register_14_q, register_15_q;

  Demultiplexer #(.select(4)) demultiplexer_1 (
    .out1(demultiplexer_1_out1), .out2(demultiplexer_1_out2), .out3(demultiplexer_1_out3),
    .out4(demultiplexer_1_out4), .out5(demultiplexer_1_out5), .out6(demultiplexer_1_out6),
    .out7(demultiplexer_1_out7), .out8(demultiplexer_1_out8), .out9(demultiplexer_1_out9),
    .out10(demultiplexer_1_out10), .out11(demultiplexer_1_out11), .out12(demultiplexer_1_out12),
    .out13(demultiplexer_1_out13), .out14(demultiplexer_1_out14), .out15(demultiplexer_1_out15), .in(Re),
    .sel(Rwa));  // open: out0
  Register register_1 (.D(Rwd), .en(demultiplexer_1_out1), .clk(Rc), .Q(register_1_q), .clr(Rr));
  Register register_2 (.D(Rwd), .en(demultiplexer_1_out2), .clk(Rc), .Q(register_2_q), .clr(Rr));
  Register register_3 (.D(Rwd), .en(demultiplexer_1_out3), .clk(Rc), .Q(register_3_q), .clr(Rr));
  Register register_4 (.D(Rwd), .en(demultiplexer_1_out4), .clk(Rc), .Q(register_4_q), .clr(Rr));
  Register register_5 (.D(Rwd), .en(demultiplexer_1_out5), .clk(Rc), .Q(register_5_q), .clr(Rr));
  Register register_6 (.D(Rwd), .en(demultiplexer_1_out6), .clk(Rc), .Q(register_6_q), .clr(Rr));
  Register register_7 (.D(Rwd), .en(demultiplexer_1_out7), .clk(Rc), .Q(register_7_q), .clr(Rr));
  Register register_8 (.D(Rwd), .en(demultiplexer_1_out8), .clk(Rc), .Q(register_8_q), .clr(Rr));
  Register register_9 (.D(Rwd), .en(demultiplexer_1_out9), .clk(Rc), .Q(register_9_q), .clr(Rr));
  Register register_10 (.D(Rwd), .en(demultiplexer_1_out10), .clk(Rc), .Q(register_10_q), .clr(Rr));
  Register register_11 (.D(Rwd), .en(demultiplexer_1_out11), .clk(Rc), .Q(register_11_q), .clr(Rr));
  Register register_12 (.D(Rwd), .en(demultiplexer_1_out12), .clk(Rc), .Q(register_12_q), .clr(Rr));
  Register register_13 (.D(Rwd), .en(demultiplexer_1_out13), .clk(Rc), .Q(register_13_q), .clr(Rr));
  Register register_14 (.D(Rwd), .en(demultiplexer_1_out14), .clk(Rc), .Q(register_14_q), .clr(Rr));
  Register register_15 (.D(Rwd), .en(demultiplexer_1_out15), .clk(Rc), .Q(register_15_q), .clr(Rr));
  Multiplexer #(.select(4), .width(8)) multiplexer_1 (
    .in0({8{1'b0}}), .in1(register_1_q), .in2(register_2_q), .in3(register_3_q), .in4(register_4_q),
    .in5(register_5_q), .in6(register_6_q), .in7(register_7_q), .in8(register_8_q), .in9(register_9_q),
    .in10(register_10_q), .in11(register_11_q), .in12(register_12_q), .in13(register_13_q),
    .in14(register_14_q), .in15(register_15_q), .out(multiplexer_1_out), .sel(Rra0));
  Multiplexer #(.select(4), .width(8)) multiplexer_2 (
    .in0({8{1'b0}}), .in1(register_1_q), .in2(register_2_q), .in3(register_3_q), .in4(register_4_q),
    .in5(register_5_q), .in6(register_6_q), .in7(register_7_q), .in8(register_8_q), .in9(register_9_q),
    .in10(register_10_q), .in11(register_11_q), .in12(register_12_q), .in13(register_13_q),
    .in14(register_14_q), .in15(register_15_q), .out(multiplexer_2_out), .sel(Rra1));
  Multiplexer #(.width(8)) multiplexer_3 (.in0({8{1'b0}}), .in1(multiplexer_1_out), .out(Rrd0), .sel(Re));
  Multiplexer #(.width(8)) multiplexer_4 (.in0({8{1'b0}}), .in1(multiplexer_2_out), .out(Rrd1), .sel(Re));
endmodule

module ALU (
  input  [7:0] ALUw0,
  input  [7:0] ALUw1,
  input  ALUd0,
  input  ALUd1,
  input  ALUd2,
  input  [1:0] ALUfi,
  input  ALUc,
  output [7:0] ALUr,
  output ALUfo
);

  wire adder_1_cout, bitselector_4_out, bitselector_5_out, bitselector_6_out, bitselector_7_out,
       bitselector_8_out, bitselector_9_out, bitselector_10_out, bitselector_11_out, d_ff_1_q, d_ff_1_qn,
       d_ff_2_q, d_ff_2_qn, multiplexer_2_out, or_2_out, subtractor_1_bout;
  wire [2:0] bitselector_1_out, bitselector_2_out, bitselector_3_out, or_1_out, shifter_2_out, shifter_3_out;
  wire [7:0] adder_1_out, and_1_out, nor_1_out, shifter_1_out, subtractor_1_out, xor_1_out;

  BitSelector #(.group(3), .width(1)) bitselector_1 (.in(ALUd0), .out(bitselector_1_out), .sel(1'b0));
  BitSelector #(.group(3), .width(1)) bitselector_2 (.in(ALUd1), .out(bitselector_2_out), .sel(1'b0));
  BitSelector #(.group(3), .width(1)) bitselector_3 (.in(ALUd2), .out(bitselector_3_out), .sel(1'b0));
  Adder adder_1 (.a(ALUw0), .b(ALUw1), .out(adder_1_out), .cout(adder_1_cout));  // open: cin
  Subtractor subtractor_1 (.a(ALUw0), .b(ALUw1), .out(subtractor_1_out), .bout(subtractor_1_bout));  // open: bin
  assign nor_1_out = ~(ALUw0 | ALUw1);  // NOR_Gate nor_1, 8 bits wide
  assign and_1_out = ALUw0 & ALUw1;  // AND_Gate and_1, 8 bits wide
  assign xor_1_out = ALUw0 ^ ALUw1;  // XOR_Gate xor_1, 8 bits wide
  Shifter #(.shift("lr")) shifter_1 (.in(ALUw0), .\dist (3'b001), .out(shifter_1_out));
  Shifter #(.width(3)) shifter_2 (.in(bitselector_2_out), .\dist (2'b01), .out(shifter_2_out));
  Shifter #(.width(3)) shifter_3 (.in(bitselector_3_out), .\dist (2'b10), .out(shifter_3_out));
  Multiplexer #(.select(3), .width(8)) multiplexer_1 (
    .in0(adder_1_out), .in1(subtractor_1_out), .in2(nor_1_out), .in3(and_1_out), .in4(xor_1_out),
    .in5(shifter_1_out), .out(ALUr), .sel(or_1_out));  // open: in6, in7
  assign or_1_out = bitselector_1_out | shifter_2_out | shifter_3_out;  // OR_Gate or_1, 3 bits wide
  Multiplexer #(.select(3)) multiplexer_2 (
    .in0(adder_1_cout), .in1(subtractor_1_bout), .in2(1'b0), .in3(1'b0), .in4(1'b0), .in5(1'b0), .in6(1'b0),
    .in7(1'b0), .out(multiplexer_2_out), .sel(or_1_out));
  D_Flip_Flop d_ff_1 (.D(multiplexer_2_out), .clk(ALUc), .Q(d_ff_1_q), .Qn(d_ff_1_qn));  // open: preset, reset
  D_Flip_Flop d_ff_2 (.D(or_2_out), .clk(ALUc), .Q(d_ff_2_q), .Qn(d_ff_2_qn));  // open: preset, reset
  BitSelector bitselector_4 (.in(ALUr), .out(bitselector_4_out), .sel(3'b110));
  BitSelector bitselector_5 (.in(ALUr), .out(bitselector_5_out), .sel(3'b100));
  BitSelector bitselector_6 (.in(ALUr), .out(bitselector_6_out), .sel(3'b010));
  BitSelector bitselector_7 (.in(ALUr), .out(bitselector_7_out), .sel(3'b000));
  BitSelector bitselector_8 (.in(ALUr), .out(bitselector_8_out), .sel(3'b111));
  BitSelector bitselector_9 (.in(ALUr), .out(bitselector_9_out), .sel(3'b101));
  BitSelector bitselector_10 (.in(ALUr), .out(bitselector_10_out), .sel(3'b011));
  BitSelector bitselector_11 (.in(ALUr), .out(bitselector_11_out), .sel(3'b001));
  or or_2 (or_2_out, bitselector_7_out, bitselector_6_out, bitselector_5_out, bitselector_4_out, bitselector_11_out, bitselector_10_out, bitselector_9_out, bitselector_8_out);
  Multiplexer #(.select(2)) multiplexer_3 (
    .in0(d_ff_2_qn), .in1(d_ff_2_q), .in2(d_ff_1_qn), .in3(d_ff_1_q), .out(ALUfo), .sel(ALUfi));
endmodule

module PC (
  input  [9:0] PCd0,
  input  [9:0] PCd1,
  input  PCd2,
  input  PCa0,
  input  PCa1,
  input  PCa2,
  input  PCh,
  input  PCc,
  input  PCr,
  output PCt,
  output [9:0] PCc0
);

  wire and_1_out, multiplexer_1_out, not_1_out, not_2_out, not_3_out, or_1_out;
  wire [1:0] multiplexer_2_out, multiplexer_3_out, or_2_out;
  wire [9:0] adder_1_out, multiplexer_4_out;

  Multiplexer multiplexer_1 (.in0(1'b0), .in1(PCd2), .out(multiplexer_1_out), .sel(PCa0));
  or or_1 (or_1_out, multiplexer_1_out, PCa1);
  Multiplexer #(.width(2)) multiplexer_2 (.in0(2'b00), .in1(2'b01), .out(multiplexer_2_out), .sel(or_1_out));
  Multiplexer #(.width(2)) multiplexer_3 (.in0(2'b00), .in1(2'b10), .out(multiplexer_3_out), .sel(PCa2));
  Multiplexer #(.select(2), .width(10)) multiplexer_4 (
    .in0(adder_1_out), .in1(PCd0), .in2(PCd1), .out(multiplexer_4_out), .sel(or_2_out));  // open: in3
  assign or_2_out = multiplexer_2_out | multiplexer_3_out;  // OR_Gate or_2, 2 bits wide
  and and_1 (and_1_out, PCc, not_3_out);
  Register #(.width(10)) register_1 (.D(multiplexer_4_out), .en(1'b1), .clk(not_1_out), .Q(PCc0), .clr(PCr));
  not not_1 (not_1_out, PCt);
  and and_2 (PCt, and_1_out, not_2_out);
  not not_2 (not_2_out, PCr);
  not not_3 (not_3_out, PCh);
  Adder #(.width(10)) adder_1 (.a(10'h1), .b(PCc0), .out(adder_1_out));  // open: cin, cout
endmodule
